// Digital circuit 16-bit Barrel-Shifter.dig as structural Verilog
module _16_bit_Barrel_Shifter (
  input  [15:0] D,
  input  BRE,
  input  L_R,
  input  CE,
  input  [3:0] SHC,
  input  RCE,
  input  Cin,
  input  AE,
  input  Mod,
  output [15:0] Q,
  output CO
);

  wire and_2_out, and_3_out, and_4_out, and_5_out, and_6_out, and_7_out, and_8_out, and_9_out, and_10_out,
       and_11_out, and_12_out, and_13_out, and_14_out, and_15_out, and_16_out, and_17_out, and_18_out,
       and_19_out, and_20_out, and_21_out, and_22_out, and_23_out, and_24_out, and_25_out, and_26_out,
       and_27_out, and_28_out, and_29_out, and_30_out, and_31_out, b, c, decoder_1_out_0, decoder_1_out_1,
       delay_1_out, driver_1_out, driver_3_out, driver_5_out, driver_7_out, driver_9_out, driver_11_out,
       driver_13_out, driver_15_out, driver_17_out, driver_19_out, driver_21_out, driver_23_out,
       driver_25_out, driver_27_out, driver_29_out, driver_31_out, driver_33_out, driver_35_out,
       driver_62_out, driver_63_out, driver_68_out, driver_84_out, driver_87_out, driver_88_out,
       driver_125_out, driver_126_out, driver_146_out, driver_147_out, driver_152_out, driver_168_out,
       driver_171_out, driver_172_out, driver_209_out, driver_210_out, driver_230_out, driver_231_out,
       driver_236_out, driver_252_out, driver_255_out, driver_256_out, driver_292_out, driver_293_out,
       driver_314_out, driver_315_out, driver_320_out, driver_336_out, driver_339_out, driver_340_out,
       driver_376_out, driver_377_out, multiplexer_2_out, multiplexer_3_out, multiplexer_4_out,
       multiplexer_5_out, multiplexer_6_out, multiplexer_7_out, multiplexer_8_out, multiplexer_9_out,
       not_1_out, not_2_out, not_3_out, or_1_out, or_2_out, or_3_out, or_4_out, or_5_out, or_6_out, or_7_out,
       or_8_out, or_9_out, or_10_out, or_11_out, pulldown_1_out, pulldown_2_out, pulldown_3_out,
       pulldown_4_out, pulldown_5_out, pulldown_6_out, pulldown_7_out, pulldown_8_out, pulldown_9_out,
       pulldown_10_out, pulldown_11_out, ShiftBits;
  wire [3:0] pulldown_41_out;
  wire [15:0] Conf, Conf2, decoder_2_out_15, driver_44_out, Out, Out2;
  wire [15:1] multiplexer_12_out;

  not not_1 (not_1_out, L_R);
  and and_1 (ShiftBits, not_1_out, Mod);
  and and_2 (and_2_out, BRE, delay_1_out);
  and and_3 (and_3_out, BRE, not_2_out);
  not not_2 (not_2_out, RCE);
  Delay delay_1 (.in(RCE), .out(delay_1_out));
  Decoder decoder_1 (.sel(RCE), .out_0(decoder_1_out_0), .out_1(decoder_1_out_1));
  Decoder #(.Selector_Bits(4)) decoder_2 (
    .sel(SHC), .out_0(decoder_2_out_15[0]), .out_1(decoder_2_out_15[1]), .out_2(decoder_2_out_15[2]),
    .out_3(decoder_2_out_15[3]), .out_4(decoder_2_out_15[4]), .out_5(decoder_2_out_15[5]),
    .out_6(decoder_2_out_15[6]), .out_7(decoder_2_out_15[7]), .out_8(decoder_2_out_15[8]),
    .out_9(decoder_2_out_15[9]), .out_10(decoder_2_out_15[10]), .out_11(decoder_2_out_15[11]),
    .out_12(decoder_2_out_15[12]), .out_13(decoder_2_out_15[13]), .out_14(decoder_2_out_15[14]),
    .out_15(decoder_2_out_15[15]));
  Multiplexer #(.Bits(16)) multiplexer_1 (
    .sel(L_R), .in_0(D),
    .in_1({D[0], D[1], D[2], D[3], D[4], D[5], D[6], D[7], D[8], D[9], D[10], D[11], D[12], D[13], D[14], D[15]}),
    .out(Out));
  assign driver_1_out = decoder_1_out_1 ? Cin : 1'bz;  // Driver driver_1
  PullDown pulldown_1 (.out(pulldown_1_out));
  assign pulldown_1_out = decoder_1_out_0 ? decoder_2_out_15[15] : 1'bz;  // Driver driver_2
  assign driver_3_out = decoder_1_out_1 ? decoder_2_out_15[15] : 1'bz;  // Driver driver_3
  assign driver_3_out = decoder_1_out_0 ? decoder_2_out_15[14] : 1'bz;  // Driver driver_4
  assign driver_5_out = decoder_1_out_1 ? decoder_2_out_15[14] : 1'bz;  // Driver driver_5
  assign driver_5_out = decoder_1_out_0 ? decoder_2_out_15[13] : 1'bz;  // Driver driver_6
  assign driver_7_out = decoder_1_out_1 ? decoder_2_out_15[13] : 1'bz;  // Driver driver_7
  assign driver_7_out = decoder_1_out_0 ? decoder_2_out_15[12] : 1'bz;  // Driver driver_8
  assign driver_9_out = decoder_1_out_1 ? decoder_2_out_15[12] : 1'bz;  // Driver driver_9
  assign driver_9_out = decoder_1_out_0 ? decoder_2_out_15[11] : 1'bz;  // Driver driver_10
  assign driver_11_out = decoder_1_out_1 ? decoder_2_out_15[11] : 1'bz;  // Driver driver_11
  assign driver_11_out = decoder_1_out_0 ? decoder_2_out_15[10] : 1'bz;  // Driver driver_12
  assign driver_13_out = decoder_1_out_1 ? decoder_2_out_15[10] : 1'bz;  // Driver driver_13
  assign driver_13_out = decoder_1_out_0 ? decoder_2_out_15[9] : 1'bz;  // Driver driver_14
  assign driver_15_out = decoder_1_out_1 ? decoder_2_out_15[9] : 1'bz;  // Driver driver_15
  assign driver_15_out = decoder_1_out_0 ? decoder_2_out_15[8] : 1'bz;  // Driver driver_16
  assign driver_17_out = decoder_1_out_1 ? decoder_2_out_15[8] : 1'bz;  // Driver driver_17
  assign driver_17_out = decoder_1_out_0 ? decoder_2_out_15[7] : 1'bz;  // Driver driver_18
  assign driver_19_out = decoder_1_out_1 ? decoder_2_out_15[7] : 1'bz;  // Driver driver_19
  assign driver_19_out = decoder_1_out_0 ? decoder_2_out_15[6] : 1'bz;  // Driver driver_20
  assign driver_21_out = decoder_1_out_1 ? decoder_2_out_15[6] : 1'bz;  // Driver driver_21
  assign driver_21_out = decoder_1_out_0 ? decoder_2_out_15[5] : 1'bz;  // Driver driver_22
  assign driver_23_out = decoder_1_out_1 ? decoder_2_out_15[5] : 1'bz;  // Driver driver_23
  assign driver_23_out = decoder_1_out_0 ? decoder_2_out_15[4] : 1'bz;  // Driver driver_24
  assign driver_25_out = decoder_1_out_1 ? decoder_2_out_15[4] : 1'bz;  // Driver driver_25
  assign driver_25_out = decoder_1_out_0 ? decoder_2_out_15[3] : 1'bz;  // Driver driver_26
  assign driver_27_out = decoder_1_out_1 ? decoder_2_out_15[3] : 1'bz;  // Driver driver_27
  assign driver_27_out = decoder_1_out_0 ? decoder_2_out_15[2] : 1'bz;  // Driver driver_28
  assign driver_29_out = decoder_1_out_1 ? decoder_2_out_15[2] : 1'bz;  // Driver driver_29
  assign driver_29_out = decoder_1_out_0 ? decoder_2_out_15[1] : 1'bz;  // Driver driver_30
  assign driver_31_out = decoder_1_out_1 ? decoder_2_out_15[1] : 1'bz;  // Driver driver_31
  assign driver_31_out = decoder_1_out_0 ? decoder_2_out_15[0] : 1'bz;  // Driver driver_32
  assign driver_33_out = AE ? D[15] : 1'bz;  // Driver driver_33
  assign driver_1_out = decoder_1_out_0 ? Conf[0] : 1'bz;  // Driver driver_34
  assign driver_35_out = 1'b0 ? driver_1_out : 1'bz;  // Driver driver_35
  assign driver_44_out[0] = pulldown_1_out ? driver_1_out : 1'bz;  // Driver driver_36
  assign driver_44_out[1] = driver_3_out ? driver_1_out : 1'bz;  // Driver driver_37
  assign driver_44_out[2] = driver_5_out ? driver_1_out : 1'bz;  // Driver driver_38
  assign driver_44_out[3] = driver_7_out ? driver_1_out : 1'bz;  // Driver driver_39
  assign driver_44_out[4] = driver_9_out ? driver_1_out : 1'bz;  // Driver driver_40
  assign driver_44_out[5] = driver_11_out ? driver_1_out : 1'bz;  // Driver driver_41
  assign driver_44_out[6] = pulldown_2_out ? driver_1_out : 1'bz;  // Driver driver_42
  PullDown pulldown_2 (.out(pulldown_2_out));
  assign pulldown_2_out = not_3_out ? driver_13_out : 1'bz;  // Driver driver_43
  assign driver_44_out[7] = pulldown_3_out ? driver_1_out : 1'bz;  // Driver driver_44
  PullDown pulldown_3 (.out(pulldown_3_out));
  assign pulldown_3_out = not_3_out ? driver_15_out : 1'bz;  // Driver driver_45
  assign driver_44_out[8] = pulldown_4_out ? driver_1_out : 1'bz;  // Driver driver_46
  PullDown pulldown_4 (.out(pulldown_4_out));
  assign pulldown_4_out = not_3_out ? driver_17_out : 1'bz;  // Driver driver_47
  assign driver_44_out[9] = pulldown_5_out ? driver_1_out : 1'bz;  // Driver driver_48
  PullDown pulldown_5 (.out(pulldown_5_out));
  assign pulldown_5_out = not_3_out ? driver_19_out : 1'bz;  // Driver driver_49
  assign driver_44_out[10] = pulldown_6_out ? driver_1_out : 1'bz;  // Driver driver_50
  PullDown pulldown_6 (.out(pulldown_6_out));
  assign pulldown_6_out = not_3_out ? driver_21_out : 1'bz;  // Driver driver_51
  assign driver_44_out[11] = pulldown_7_out ? driver_1_out : 1'bz;  // Driver driver_52
  PullDown pulldown_7 (.out(pulldown_7_out));
  assign pulldown_7_out = not_3_out ? driver_23_out : 1'bz;  // Driver driver_53
  assign driver_44_out[12] = pulldown_8_out ? driver_1_out : 1'bz;  // Driver driver_54
  PullDown pulldown_8 (.out(pulldown_8_out));
  assign pulldown_8_out = not_3_out ? driver_25_out : 1'bz;  // Driver driver_55
  assign driver_44_out[13] = pulldown_9_out ? driver_1_out : 1'bz;  // Driver driver_56
  PullDown pulldown_9 (.out(pulldown_9_out));
  assign pulldown_9_out = not_3_out ? driver_27_out : 1'bz;  // Driver driver_57
  assign driver_44_out[14] = pulldown_10_out ? driver_1_out : 1'bz;  // Driver driver_58
  PullDown pulldown_10 (.out(pulldown_10_out));
  assign pulldown_10_out = not_3_out ? driver_29_out : 1'bz;  // Driver driver_59
  assign driver_44_out[15] = pulldown_11_out ? driver_1_out : 1'bz;  // Driver driver_60
  PullDown pulldown_11 (.out(pulldown_11_out));
  assign pulldown_11_out = not_3_out ? driver_31_out : 1'bz;  // Driver driver_61
  assign driver_62_out = decoder_1_out_1 ? Conf[0] : 1'bz;  // Driver driver_62
  assign driver_63_out = and_2_out ? 1'b0 : 1'bz;  // Driver driver_63
  PullDown pulldown_12 (.out(driver_35_out));
  PullDown pulldown_13 (.out(driver_63_out));
  PullDown pulldown_14 (.out(driver_44_out[0]));
  assign driver_63_out = and_3_out ? pulldown_1_out : 1'bz;  // Driver driver_64
  PullDown pulldown_15 (.out(driver_44_out[1]));
  PullDown pulldown_16 (.out(driver_44_out[2]));
  PullDown pulldown_17 (.out(driver_44_out[3]));
  PullDown pulldown_18 (.out(driver_44_out[4]));
  PullDown pulldown_19 (.out(driver_44_out[5]));
  assign driver_62_out = decoder_1_out_0 ? Conf[1] : 1'bz;  // Driver driver_65
  assign driver_35_out = pulldown_1_out ? driver_62_out : 1'bz;  // Driver driver_66
  assign driver_44_out[0] = driver_3_out ? driver_62_out : 1'bz;  // Driver driver_67
  assign driver_68_out = and_3_out ? driver_3_out : 1'bz;  // Driver driver_68
  assign driver_44_out[1] = driver_5_out ? driver_62_out : 1'bz;  // Driver driver_69
  assign driver_44_out[2] = driver_7_out ? driver_62_out : 1'bz;  // Driver driver_70
  assign driver_44_out[3] = driver_9_out ? driver_62_out : 1'bz;  // Driver driver_71
  assign driver_44_out[4] = driver_11_out ? driver_62_out : 1'bz;  // Driver driver_72
  assign driver_44_out[5] = pulldown_2_out ? driver_62_out : 1'bz;  // Driver driver_73
  assign driver_44_out[6] = pulldown_3_out ? driver_62_out : 1'bz;  // Driver driver_74
  PullDown pulldown_20 (.out(driver_44_out[6]));
  assign driver_44_out[7] = pulldown_4_out ? driver_62_out : 1'bz;  // Driver driver_75
  PullDown pulldown_21 (.out(driver_44_out[7]));
  assign driver_44_out[8] = pulldown_5_out ? driver_62_out : 1'bz;  // Driver driver_76
  assign driver_44_out[9] = pulldown_6_out ? driver_62_out : 1'bz;  // Driver driver_77
  assign driver_44_out[10] = pulldown_7_out ? driver_62_out : 1'bz;  // Driver driver_78
  assign driver_44_out[11] = pulldown_8_out ? driver_62_out : 1'bz;  // Driver driver_79
  assign driver_44_out[12] = pulldown_9_out ? driver_62_out : 1'bz;  // Driver driver_80
  assign driver_44_out[13] = pulldown_10_out ? driver_62_out : 1'bz;  // Driver driver_81
  assign driver_44_out[14] = pulldown_11_out ? driver_62_out : 1'bz;  // Driver driver_82
  assign driver_44_out[15] = driver_63_out ? driver_62_out : 1'bz;  // Driver driver_83
  assign driver_84_out = decoder_1_out_1 ? Conf[1] : 1'bz;  // Driver driver_84
  assign driver_84_out = decoder_1_out_0 ? Conf[2] : 1'bz;  // Driver driver_85
  assign driver_68_out = and_2_out ? pulldown_1_out : 1'bz;  // Driver driver_86
  PullDown pulldown_22 (.out(driver_68_out));
  PullDown pulldown_23 (.out(driver_44_out[15]));
  assign driver_87_out = decoder_1_out_1 ? Conf[2] : 1'bz;  // Driver driver_87
  assign driver_88_out = and_2_out ? driver_3_out : 1'bz;  // Driver driver_88
  assign driver_35_out = driver_3_out ? driver_84_out : 1'bz;  // Driver driver_89
  PullDown pulldown_24 (.out(driver_88_out));
  assign driver_44_out[0] = driver_5_out ? driver_84_out : 1'bz;  // Driver driver_90
  assign driver_88_out = and_3_out ? driver_5_out : 1'bz;  // Driver driver_91
  assign driver_44_out[1] = driver_7_out ? driver_84_out : 1'bz;  // Driver driver_92
  assign driver_44_out[2] = driver_9_out ? driver_84_out : 1'bz;  // Driver driver_93
  assign driver_44_out[3] = driver_11_out ? driver_84_out : 1'bz;  // Driver driver_94
  assign driver_44_out[4] = pulldown_2_out ? driver_84_out : 1'bz;  // Driver driver_95
  assign driver_44_out[5] = pulldown_3_out ? driver_84_out : 1'bz;  // Driver driver_96
  assign driver_44_out[6] = pulldown_4_out ? driver_84_out : 1'bz;  // Driver driver_97
  assign driver_44_out[7] = pulldown_5_out ? driver_84_out : 1'bz;  // Driver driver_98
  assign driver_44_out[8] = pulldown_6_out ? driver_84_out : 1'bz;  // Driver driver_99
  assign driver_44_out[9] = pulldown_7_out ? driver_84_out : 1'bz;  // Driver driver_100
  assign driver_44_out[10] = pulldown_8_out ? driver_84_out : 1'bz;  // Driver driver_101
  assign driver_44_out[11] = pulldown_9_out ? driver_84_out : 1'bz;  // Driver driver_102
  assign driver_44_out[12] = pulldown_10_out ? driver_84_out : 1'bz;  // Driver driver_103
  assign driver_44_out[13] = pulldown_11_out ? driver_84_out : 1'bz;  // Driver driver_104
  assign driver_44_out[14] = driver_63_out ? driver_84_out : 1'bz;  // Driver driver_105
  assign driver_44_out[15] = driver_68_out ? driver_84_out : 1'bz;  // Driver driver_106
  assign driver_87_out = decoder_1_out_0 ? Conf[3] : 1'bz;  // Driver driver_107
  assign driver_35_out = driver_5_out ? driver_87_out : 1'bz;  // Driver driver_108
  assign driver_44_out[0] = driver_7_out ? driver_87_out : 1'bz;  // Driver driver_109
  assign driver_44_out[1] = driver_9_out ? driver_87_out : 1'bz;  // Driver driver_110
  assign driver_44_out[2] = driver_11_out ? driver_87_out : 1'bz;  // Driver driver_111
  assign driver_44_out[3] = pulldown_2_out ? driver_87_out : 1'bz;  // Driver driver_112
  assign driver_44_out[4] = pulldown_3_out ? driver_87_out : 1'bz;  // Driver driver_113
  assign driver_44_out[5] = pulldown_4_out ? driver_87_out : 1'bz;  // Driver driver_114
  assign driver_44_out[6] = pulldown_5_out ? driver_87_out : 1'bz;  // Driver driver_115
  assign driver_44_out[7] = pulldown_6_out ? driver_87_out : 1'bz;  // Driver driver_116
  assign driver_44_out[8] = pulldown_7_out ? driver_87_out : 1'bz;  // Driver driver_117
  assign driver_44_out[9] = pulldown_8_out ? driver_87_out : 1'bz;  // Driver driver_118
  assign driver_44_out[10] = pulldown_9_out ? driver_87_out : 1'bz;  // Driver driver_119
  assign driver_44_out[11] = pulldown_10_out ? driver_87_out : 1'bz;  // Driver driver_120
  assign driver_44_out[12] = pulldown_11_out ? driver_87_out : 1'bz;  // Driver driver_121
  assign driver_44_out[13] = driver_63_out ? driver_87_out : 1'bz;  // Driver driver_122
  assign driver_44_out[14] = driver_68_out ? driver_87_out : 1'bz;  // Driver driver_123
  assign driver_44_out[15] = driver_88_out ? driver_87_out : 1'bz;  // Driver driver_124
  assign driver_125_out = decoder_1_out_1 ? Conf[3] : 1'bz;  // Driver driver_125
  assign driver_126_out = and_2_out ? driver_5_out : 1'bz;  // Driver driver_126
  PullDown pulldown_25 (.out(driver_126_out));
  assign driver_126_out = and_3_out ? driver_7_out : 1'bz;  // Driver driver_127
  assign driver_125_out = decoder_1_out_0 ? Conf[4] : 1'bz;  // Driver driver_128
  assign driver_35_out = driver_7_out ? driver_125_out : 1'bz;  // Driver driver_129
  assign driver_44_out[0] = driver_9_out ? driver_125_out : 1'bz;  // Driver driver_130
  assign driver_44_out[1] = driver_11_out ? driver_125_out : 1'bz;  // Driver driver_131
  assign driver_44_out[2] = pulldown_2_out ? driver_125_out : 1'bz;  // Driver driver_132
  assign driver_44_out[3] = pulldown_3_out ? driver_125_out : 1'bz;  // Driver driver_133
  assign driver_44_out[4] = pulldown_4_out ? driver_125_out : 1'bz;  // Driver driver_134
  assign driver_44_out[5] = pulldown_5_out ? driver_125_out : 1'bz;  // Driver driver_135
  assign driver_44_out[6] = pulldown_6_out ? driver_125_out : 1'bz;  // Driver driver_136
  assign driver_44_out[7] = pulldown_7_out ? driver_125_out : 1'bz;  // Driver driver_137
  assign driver_44_out[8] = pulldown_8_out ? driver_125_out : 1'bz;  // Driver driver_138
  assign driver_44_out[9] = pulldown_9_out ? driver_125_out : 1'bz;  // Driver driver_139
  assign driver_44_out[10] = pulldown_10_out ? driver_125_out : 1'bz;  // Driver driver_140
  assign driver_44_out[11] = pulldown_11_out ? driver_125_out : 1'bz;  // Driver driver_141
  assign driver_44_out[12] = driver_63_out ? driver_125_out : 1'bz;  // Driver driver_142
  assign driver_44_out[13] = driver_68_out ? driver_125_out : 1'bz;  // Driver driver_143
  assign driver_44_out[14] = driver_88_out ? driver_125_out : 1'bz;  // Driver driver_144
  assign driver_44_out[15] = driver_126_out ? driver_125_out : 1'bz;  // Driver driver_145
  assign driver_146_out = decoder_1_out_1 ? Conf[4] : 1'bz;  // Driver driver_146
  assign driver_147_out = and_2_out ? driver_7_out : 1'bz;  // Driver driver_147
  PullDown pulldown_26 (.out(driver_147_out));
  assign driver_147_out = and_3_out ? driver_9_out : 1'bz;  // Driver driver_148
  assign driver_146_out = decoder_1_out_0 ? Conf[5] : 1'bz;  // Driver driver_149
  assign driver_35_out = driver_9_out ? driver_146_out : 1'bz;  // Driver driver_150
  assign driver_44_out[0] = driver_11_out ? driver_146_out : 1'bz;  // Driver driver_151
  assign driver_152_out = and_3_out ? driver_11_out : 1'bz;  // Driver driver_152
  assign driver_44_out[1] = pulldown_2_out ? driver_146_out : 1'bz;  // Driver driver_153
  assign driver_44_out[2] = pulldown_3_out ? driver_146_out : 1'bz;  // Driver driver_154
  assign driver_44_out[3] = pulldown_4_out ? driver_146_out : 1'bz;  // Driver driver_155
  assign driver_44_out[4] = pulldown_5_out ? driver_146_out : 1'bz;  // Driver driver_156
  assign driver_44_out[5] = pulldown_6_out ? driver_146_out : 1'bz;  // Driver driver_157
  assign driver_44_out[6] = pulldown_7_out ? driver_146_out : 1'bz;  // Driver driver_158
  assign driver_44_out[7] = pulldown_8_out ? driver_146_out : 1'bz;  // Driver driver_159
  assign driver_44_out[8] = pulldown_9_out ? driver_146_out : 1'bz;  // Driver driver_160
  assign driver_44_out[9] = pulldown_10_out ? driver_146_out : 1'bz;  // Driver driver_161
  assign driver_44_out[10] = pulldown_11_out ? driver_146_out : 1'bz;  // Driver driver_162
  assign driver_44_out[11] = driver_63_out ? driver_146_out : 1'bz;  // Driver driver_163
  assign driver_44_out[12] = driver_68_out ? driver_146_out : 1'bz;  // Driver driver_164
  assign driver_44_out[13] = driver_88_out ? driver_146_out : 1'bz;  // Driver driver_165
  assign driver_44_out[14] = driver_126_out ? driver_146_out : 1'bz;  // Driver driver_166
  assign driver_44_out[15] = driver_147_out ? driver_146_out : 1'bz;  // Driver driver_167
  assign driver_168_out = decoder_1_out_1 ? Conf[5] : 1'bz;  // Driver driver_168
  assign driver_168_out = decoder_1_out_0 ? Conf[6] : 1'bz;  // Driver driver_169
  assign driver_152_out = and_2_out ? driver_9_out : 1'bz;  // Driver driver_170
  PullDown pulldown_27 (.out(driver_152_out));
  assign driver_171_out = decoder_1_out_1 ? Conf[6] : 1'bz;  // Driver driver_171
  assign driver_172_out = and_2_out ? driver_11_out : 1'bz;  // Driver driver_172
  assign driver_35_out = driver_11_out ? driver_168_out : 1'bz;  // Driver driver_173
  PullDown pulldown_28 (.out(driver_172_out));
  assign driver_44_out[0] = pulldown_2_out ? driver_168_out : 1'bz;  // Driver driver_174
  assign driver_172_out = and_3_out ? pulldown_2_out : 1'bz;  // Driver driver_175
  assign driver_44_out[1] = pulldown_3_out ? driver_168_out : 1'bz;  // Driver driver_176
  assign driver_44_out[2] = pulldown_4_out ? driver_168_out : 1'bz;  // Driver driver_177
  assign driver_44_out[3] = pulldown_5_out ? driver_168_out : 1'bz;  // Driver driver_178
  assign driver_44_out[4] = pulldown_6_out ? driver_168_out : 1'bz;  // Driver driver_179
  assign driver_44_out[5] = pulldown_7_out ? driver_168_out : 1'bz;  // Driver driver_180
  assign driver_44_out[6] = pulldown_8_out ? driver_168_out : 1'bz;  // Driver driver_181
  assign driver_44_out[7] = pulldown_9_out ? driver_168_out : 1'bz;  // Driver driver_182
  assign driver_44_out[8] = pulldown_10_out ? driver_168_out : 1'bz;  // Driver driver_183
  assign driver_44_out[9] = pulldown_11_out ? driver_168_out : 1'bz;  // Driver driver_184
  assign driver_44_out[10] = driver_63_out ? driver_168_out : 1'bz;  // Driver driver_185
  assign driver_44_out[11] = driver_68_out ? driver_168_out : 1'bz;  // Driver driver_186
  assign driver_44_out[12] = driver_88_out ? driver_168_out : 1'bz;  // Driver driver_187
  assign driver_44_out[13] = driver_126_out ? driver_168_out : 1'bz;  // Driver driver_188
  assign driver_44_out[14] = driver_147_out ? driver_168_out : 1'bz;  // Driver driver_189
  assign driver_44_out[15] = driver_152_out ? driver_168_out : 1'bz;  // Driver driver_190
  assign driver_171_out = decoder_1_out_0 ? b : 1'bz;  // Driver driver_191
  assign driver_35_out = pulldown_2_out ? driver_171_out : 1'bz;  // Driver driver_192
  assign driver_44_out[0] = pulldown_3_out ? driver_171_out : 1'bz;  // Driver driver_193
  assign driver_44_out[1] = pulldown_4_out ? driver_171_out : 1'bz;  // Driver driver_194
  assign driver_44_out[2] = pulldown_5_out ? driver_171_out : 1'bz;  // Driver driver_195
  assign driver_44_out[3] = pulldown_6_out ? driver_171_out : 1'bz;  // Driver driver_196
  assign driver_44_out[4] = pulldown_7_out ? driver_171_out : 1'bz;  // Driver driver_197
  assign driver_44_out[5] = pulldown_8_out ? driver_171_out : 1'bz;  // Driver driver_198
  assign driver_44_out[6] = pulldown_9_out ? driver_171_out : 1'bz;  // Driver driver_199
  assign driver_44_out[7] = pulldown_10_out ? driver_171_out : 1'bz;  // Driver driver_200
  assign driver_44_out[8] = pulldown_11_out ? driver_171_out : 1'bz;  // Driver driver_201
  assign driver_44_out[9] = driver_63_out ? driver_171_out : 1'bz;  // Driver driver_202
  assign driver_44_out[10] = driver_68_out ? driver_171_out : 1'bz;  // Driver driver_203
  assign driver_44_out[11] = driver_88_out ? driver_171_out : 1'bz;  // Driver driver_204
  assign driver_44_out[12] = driver_126_out ? driver_171_out : 1'bz;  // Driver driver_205
  assign driver_44_out[13] = driver_147_out ? driver_171_out : 1'bz;  // Driver driver_206
  assign driver_44_out[14] = driver_152_out ? driver_171_out : 1'bz;  // Driver driver_207
  assign driver_44_out[15] = driver_172_out ? driver_171_out : 1'bz;  // Driver driver_208
  assign driver_209_out = decoder_1_out_1 ? c : 1'bz;  // Driver driver_209
  assign driver_210_out = and_2_out ? pulldown_2_out : 1'bz;  // Driver driver_210
  PullDown pulldown_29 (.out(driver_210_out));
  assign driver_210_out = and_3_out ? pulldown_3_out : 1'bz;  // Driver driver_211
  not not_3 (not_3_out, Mod);
  assign driver_209_out = decoder_1_out_0 ? Conf[8] : 1'bz;  // Driver driver_212
  assign driver_35_out = driver_15_out ? driver_209_out : 1'bz;  // Driver driver_213
  assign driver_44_out[0] = driver_17_out ? driver_209_out : 1'bz;  // Driver driver_214
  assign driver_44_out[1] = driver_19_out ? driver_209_out : 1'bz;  // Driver driver_215
  assign driver_44_out[2] = driver_21_out ? driver_209_out : 1'bz;  // Driver driver_216
  assign driver_44_out[3] = driver_23_out ? driver_209_out : 1'bz;  // Driver driver_217
  assign driver_44_out[4] = driver_25_out ? driver_209_out : 1'bz;  // Driver driver_218
  assign driver_44_out[5] = driver_27_out ? driver_209_out : 1'bz;  // Driver driver_219
  assign driver_44_out[6] = driver_29_out ? driver_209_out : 1'bz;  // Driver driver_220
  assign driver_44_out[7] = driver_31_out ? driver_209_out : 1'bz;  // Driver driver_221
  assign driver_44_out[8] = driver_63_out ? driver_209_out : 1'bz;  // Driver driver_222
  assign driver_44_out[9] = driver_68_out ? driver_209_out : 1'bz;  // Driver driver_223
  assign driver_44_out[10] = driver_88_out ? driver_209_out : 1'bz;  // Driver driver_224
  assign driver_44_out[11] = driver_126_out ? driver_209_out : 1'bz;  // Driver driver_225
  assign driver_44_out[12] = driver_147_out ? driver_209_out : 1'bz;  // Driver driver_226
  assign driver_44_out[13] = driver_152_out ? driver_209_out : 1'bz;  // Driver driver_227
  assign driver_44_out[14] = driver_172_out ? driver_209_out : 1'bz;  // Driver driver_228
  assign driver_44_out[15] = driver_210_out ? driver_209_out : 1'bz;  // Driver driver_229
  assign driver_230_out = decoder_1_out_1 ? Conf[8] : 1'bz;  // Driver driver_230
  assign driver_231_out = and_2_out ? driver_15_out : 1'bz;  // Driver driver_231
  PullDown pulldown_30 (.out(driver_231_out));
  assign driver_231_out = and_3_out ? driver_17_out : 1'bz;  // Driver driver_232
  Multiplexer multiplexer_2 (.sel(Mod), .in_0(driver_63_out), .in_1(driver_231_out), .out(multiplexer_2_out));
  assign driver_230_out = decoder_1_out_0 ? Conf[9] : 1'bz;  // Driver driver_233
  assign driver_35_out = driver_17_out ? driver_230_out : 1'bz;  // Driver driver_234
  assign driver_44_out[0] = driver_19_out ? driver_230_out : 1'bz;  // Driver driver_235
  assign driver_236_out = and_3_out ? driver_19_out : 1'bz;  // Driver driver_236
  assign driver_44_out[1] = driver_21_out ? driver_230_out : 1'bz;  // Driver driver_237
  assign driver_44_out[2] = driver_23_out ? driver_230_out : 1'bz;  // Driver driver_238
  assign driver_44_out[3] = driver_25_out ? driver_230_out : 1'bz;  // Driver driver_239
  assign driver_44_out[4] = driver_27_out ? driver_230_out : 1'bz;  // Driver driver_240
  assign driver_44_out[5] = driver_29_out ? driver_230_out : 1'bz;  // Driver driver_241
  assign driver_44_out[6] = driver_31_out ? driver_230_out : 1'bz;  // Driver driver_242
  assign driver_44_out[7] = multiplexer_2_out ? driver_230_out : 1'bz;  // Driver driver_243
  Multiplexer multiplexer_3 (.sel(Mod), .in_0(driver_68_out), .in_1(driver_236_out), .out(multiplexer_3_out));
  assign driver_44_out[8] = driver_68_out ? driver_230_out : 1'bz;  // Driver driver_244
  assign driver_44_out[9] = driver_88_out ? driver_230_out : 1'bz;  // Driver driver_245
  assign driver_44_out[10] = driver_126_out ? driver_230_out : 1'bz;  // Driver driver_246
  assign driver_44_out[11] = driver_147_out ? driver_230_out : 1'bz;  // Driver driver_247
  assign driver_44_out[12] = driver_152_out ? driver_230_out : 1'bz;  // Driver driver_248
  assign driver_44_out[13] = driver_172_out ? driver_230_out : 1'bz;  // Driver driver_249
  assign driver_44_out[14] = driver_210_out ? driver_230_out : 1'bz;  // Driver driver_250
  assign driver_44_out[15] = driver_231_out ? driver_230_out : 1'bz;  // Driver driver_251
  assign driver_252_out = decoder_1_out_1 ? Conf[9] : 1'bz;  // Driver driver_252
  assign driver_252_out = decoder_1_out_0 ? Conf[10] : 1'bz;  // Driver driver_253
  assign driver_236_out = and_2_out ? driver_17_out : 1'bz;  // Driver driver_254
  PullDown pulldown_31 (.out(driver_236_out));
  assign driver_255_out = decoder_1_out_1 ? Conf[10] : 1'bz;  // Driver driver_255
  assign driver_256_out = and_2_out ? driver_19_out : 1'bz;  // Driver driver_256
  assign driver_35_out = driver_19_out ? driver_252_out : 1'bz;  // Driver driver_257
  PullDown pulldown_32 (.out(driver_256_out));
  assign driver_44_out[0] = driver_21_out ? driver_252_out : 1'bz;  // Driver driver_258
  assign driver_256_out = and_3_out ? driver_21_out : 1'bz;  // Driver driver_259
  assign driver_44_out[1] = driver_23_out ? driver_252_out : 1'bz;  // Driver driver_260
  assign driver_44_out[2] = driver_25_out ? driver_252_out : 1'bz;  // Driver driver_261
  assign driver_44_out[3] = driver_27_out ? driver_252_out : 1'bz;  // Driver driver_262
  assign driver_44_out[4] = driver_29_out ? driver_252_out : 1'bz;  // Driver driver_263
  assign driver_44_out[5] = driver_31_out ? driver_252_out : 1'bz;  // Driver driver_264
  assign driver_44_out[6] = multiplexer_2_out ? driver_252_out : 1'bz;  // Driver driver_265
  assign driver_44_out[7] = multiplexer_3_out ? driver_252_out : 1'bz;  // Driver driver_266
  Multiplexer multiplexer_4 (.sel(Mod), .in_0(driver_88_out), .in_1(driver_256_out), .out(multiplexer_4_out));
  assign driver_44_out[8] = driver_88_out ? driver_252_out : 1'bz;  // Driver driver_267
  assign driver_44_out[9] = driver_126_out ? driver_252_out : 1'bz;  // Driver driver_268
  assign driver_44_out[10] = driver_147_out ? driver_252_out : 1'bz;  // Driver driver_269
  assign driver_44_out[11] = driver_152_out ? driver_252_out : 1'bz;  // Driver driver_270
  assign driver_44_out[12] = driver_172_out ? driver_252_out : 1'bz;  // Driver driver_271
  assign driver_44_out[13] = driver_210_out ? driver_252_out : 1'bz;  // Driver driver_272
  assign driver_44_out[14] = driver_231_out ? driver_252_out : 1'bz;  // Driver driver_273
  assign driver_44_out[15] = driver_236_out ? driver_252_out : 1'bz;  // Driver driver_274
  assign driver_255_out = decoder_1_out_0 ? Conf[11] : 1'bz;  // Driver driver_275
  assign driver_35_out = driver_21_out ? driver_255_out : 1'bz;  // Driver driver_276
  assign driver_44_out[0] = driver_23_out ? driver_255_out : 1'bz;  // Driver driver_277
  assign driver_44_out[1] = driver_25_out ? driver_255_out : 1'bz;  // Driver driver_278
  assign driver_44_out[2] = driver_27_out ? driver_255_out : 1'bz;  // Driver driver_279
  assign driver_44_out[3] = driver_29_out ? driver_255_out : 1'bz;  // Driver driver_280
  assign driver_44_out[4] = driver_31_out ? driver_255_out : 1'bz;  // Driver driver_281
  assign driver_44_out[5] = multiplexer_2_out ? driver_255_out : 1'bz;  // Driver driver_282
  assign driver_44_out[6] = multiplexer_3_out ? driver_255_out : 1'bz;  // Driver driver_283
  assign driver_44_out[8] = driver_126_out ? driver_255_out : 1'bz;  // Driver driver_284
  assign driver_44_out[9] = driver_147_out ? driver_255_out : 1'bz;  // Driver driver_285
  assign driver_44_out[10] = driver_152_out ? driver_255_out : 1'bz;  // Driver driver_286
  assign driver_44_out[11] = driver_172_out ? driver_255_out : 1'bz;  // Driver driver_287
  assign driver_44_out[12] = driver_210_out ? driver_255_out : 1'bz;  // Driver driver_288
  assign driver_44_out[13] = driver_231_out ? driver_255_out : 1'bz;  // Driver driver_289
  assign driver_44_out[14] = driver_236_out ? driver_255_out : 1'bz;  // Driver driver_290
  assign driver_44_out[15] = driver_256_out ? driver_255_out : 1'bz;  // Driver driver_291
  assign driver_292_out = decoder_1_out_1 ? Conf[11] : 1'bz;  // Driver driver_292
  assign driver_293_out = and_2_out ? driver_21_out : 1'bz;  // Driver driver_293
  PullDown pulldown_33 (.out(driver_293_out));
  assign driver_293_out = and_3_out ? driver_23_out : 1'bz;  // Driver driver_294
  assign driver_44_out[7] = multiplexer_4_out ? driver_255_out : 1'bz;  // Driver driver_295
  Multiplexer multiplexer_5 (.sel(Mod), .in_0(driver_126_out), .in_1(driver_293_out), .out(multiplexer_5_out));
  assign driver_292_out = decoder_1_out_0 ? Conf[12] : 1'bz;  // Driver driver_296
  assign driver_35_out = driver_23_out ? driver_292_out : 1'bz;  // Driver driver_297
  assign driver_44_out[0] = driver_25_out ? driver_292_out : 1'bz;  // Driver driver_298
  assign driver_44_out[1] = driver_27_out ? driver_292_out : 1'bz;  // Driver driver_299
  assign driver_44_out[2] = driver_29_out ? driver_292_out : 1'bz;  // Driver driver_300
  assign driver_44_out[3] = driver_31_out ? driver_292_out : 1'bz;  // Driver driver_301
  assign driver_44_out[4] = multiplexer_2_out ? driver_292_out : 1'bz;  // Driver driver_302
  assign driver_44_out[5] = multiplexer_3_out ? driver_292_out : 1'bz;  // Driver driver_303
  assign driver_44_out[6] = multiplexer_4_out ? driver_292_out : 1'bz;  // Driver driver_304
  assign driver_44_out[7] = multiplexer_5_out ? driver_292_out : 1'bz;  // Driver driver_305
  assign driver_44_out[8] = driver_147_out ? driver_292_out : 1'bz;  // Driver driver_306
  assign driver_44_out[9] = driver_152_out ? driver_292_out : 1'bz;  // Driver driver_307
  assign driver_44_out[10] = driver_172_out ? driver_292_out : 1'bz;  // Driver driver_308
  assign driver_44_out[11] = driver_210_out ? driver_292_out : 1'bz;  // Driver driver_309
  assign driver_44_out[12] = driver_231_out ? driver_292_out : 1'bz;  // Driver driver_310
  assign driver_44_out[13] = driver_236_out ? driver_292_out : 1'bz;  // Driver driver_311
  assign driver_44_out[14] = driver_256_out ? driver_292_out : 1'bz;  // Driver driver_312
  assign driver_44_out[15] = driver_293_out ? driver_292_out : 1'bz;  // Driver driver_313
  assign driver_314_out = decoder_1_out_1 ? Conf[12] : 1'bz;  // Driver driver_314
  assign driver_315_out = and_2_out ? driver_23_out : 1'bz;  // Driver driver_315
  PullDown pulldown_34 (.out(driver_315_out));
  assign driver_315_out = and_3_out ? driver_25_out : 1'bz;  // Driver driver_316
  Multiplexer multiplexer_6 (.sel(Mod), .in_0(driver_147_out), .in_1(driver_315_out), .out(multiplexer_6_out));
  assign driver_314_out = decoder_1_out_0 ? Conf[13] : 1'bz;  // Driver driver_317
  assign driver_35_out = driver_25_out ? driver_314_out : 1'bz;  // Driver driver_318
  assign driver_44_out[0] = driver_27_out ? driver_314_out : 1'bz;  // Driver driver_319
  assign driver_320_out = and_3_out ? driver_27_out : 1'bz;  // Driver driver_320
  assign driver_44_out[1] = driver_29_out ? driver_314_out : 1'bz;  // Driver driver_321
  assign driver_44_out[2] = driver_31_out ? driver_314_out : 1'bz;  // Driver driver_322
  assign driver_44_out[3] = multiplexer_2_out ? driver_314_out : 1'bz;  // Driver driver_323
  assign driver_44_out[4] = multiplexer_3_out ? driver_314_out : 1'bz;  // Driver driver_324
  assign driver_44_out[5] = multiplexer_4_out ? driver_314_out : 1'bz;  // Driver driver_325
  assign driver_44_out[6] = multiplexer_5_out ? driver_314_out : 1'bz;  // Driver driver_326
  assign driver_44_out[7] = multiplexer_6_out ? driver_314_out : 1'bz;  // Driver driver_327
  Multiplexer multiplexer_7 (.sel(Mod), .in_0(driver_152_out), .in_1(driver_320_out), .out(multiplexer_7_out));
  assign driver_44_out[8] = driver_152_out ? driver_314_out : 1'bz;  // Driver driver_328
  assign driver_44_out[9] = driver_172_out ? driver_314_out : 1'bz;  // Driver driver_329
  assign driver_44_out[10] = driver_210_out ? driver_314_out : 1'bz;  // Driver driver_330
  assign driver_44_out[11] = driver_231_out ? driver_314_out : 1'bz;  // Driver driver_331
  assign driver_44_out[12] = driver_236_out ? driver_314_out : 1'bz;  // Driver driver_332
  assign driver_44_out[13] = driver_256_out ? driver_314_out : 1'bz;  // Driver driver_333
  assign driver_44_out[14] = driver_293_out ? driver_314_out : 1'bz;  // Driver driver_334
  assign driver_44_out[15] = driver_315_out ? driver_314_out : 1'bz;  // Driver driver_335
  assign driver_336_out = decoder_1_out_1 ? Conf[13] : 1'bz;  // Driver driver_336
  assign driver_336_out = decoder_1_out_0 ? Conf[14] : 1'bz;  // Driver driver_337
  assign driver_320_out = and_2_out ? driver_25_out : 1'bz;  // Driver driver_338
  PullDown pulldown_35 (.out(driver_320_out));
  assign driver_339_out = decoder_1_out_1 ? Conf[14] : 1'bz;  // Driver driver_339
  assign driver_340_out = and_2_out ? driver_27_out : 1'bz;  // Driver driver_340
  assign driver_35_out = driver_27_out ? driver_336_out : 1'bz;  // Driver driver_341
  PullDown pulldown_36 (.out(driver_340_out));
  assign driver_44_out[0] = driver_29_out ? driver_336_out : 1'bz;  // Driver driver_342
  assign driver_340_out = and_3_out ? driver_29_out : 1'bz;  // Driver driver_343
  assign driver_44_out[1] = driver_31_out ? driver_336_out : 1'bz;  // Driver driver_344
  assign driver_44_out[2] = multiplexer_2_out ? driver_336_out : 1'bz;  // Driver driver_345
  assign driver_44_out[3] = multiplexer_3_out ? driver_336_out : 1'bz;  // Driver driver_346
  assign driver_44_out[4] = multiplexer_4_out ? driver_336_out : 1'bz;  // Driver driver_347
  assign driver_44_out[5] = multiplexer_5_out ? driver_336_out : 1'bz;  // Driver driver_348
  assign driver_44_out[6] = multiplexer_6_out ? driver_336_out : 1'bz;  // Driver driver_349
  assign driver_44_out[7] = multiplexer_7_out ? driver_336_out : 1'bz;  // Driver driver_350
  Multiplexer multiplexer_8 (.sel(Mod), .in_0(driver_172_out), .in_1(driver_340_out), .out(multiplexer_8_out));
  assign driver_44_out[8] = driver_172_out ? driver_336_out : 1'bz;  // Driver driver_351
  assign driver_44_out[9] = driver_210_out ? driver_336_out : 1'bz;  // Driver driver_352
  assign driver_44_out[10] = driver_231_out ? driver_336_out : 1'bz;  // Driver driver_353
  assign driver_44_out[11] = driver_236_out ? driver_336_out : 1'bz;  // Driver driver_354
  assign driver_44_out[12] = driver_256_out ? driver_336_out : 1'bz;  // Driver driver_355
  assign driver_44_out[13] = driver_293_out ? driver_336_out : 1'bz;  // Driver driver_356
  assign driver_44_out[14] = driver_315_out ? driver_336_out : 1'bz;  // Driver driver_357
  assign driver_44_out[15] = driver_320_out ? driver_336_out : 1'bz;  // Driver driver_358
  assign driver_339_out = decoder_1_out_0 ? Conf[15] : 1'bz;  // Driver driver_359
  assign driver_35_out = driver_29_out ? driver_339_out : 1'bz;  // Driver driver_360
  assign driver_44_out[0] = driver_31_out ? driver_339_out : 1'bz;  // Driver driver_361
  assign driver_44_out[1] = multiplexer_2_out ? driver_339_out : 1'bz;  // Driver driver_362
  assign driver_44_out[2] = multiplexer_3_out ? driver_339_out : 1'bz;  // Driver driver_363
  assign driver_44_out[3] = multiplexer_4_out ? driver_339_out : 1'bz;  // Driver driver_364
  assign driver_44_out[4] = multiplexer_5_out ? driver_339_out : 1'bz;  // Driver driver_365
  assign driver_44_out[5] = multiplexer_6_out ? driver_339_out : 1'bz;  // Driver driver_366
  assign driver_44_out[6] = multiplexer_7_out ? driver_339_out : 1'bz;  // Driver driver_367
  assign driver_44_out[8] = driver_210_out ? driver_339_out : 1'bz;  // Driver driver_368
  assign driver_44_out[9] = driver_231_out ? driver_339_out : 1'bz;  // Driver driver_369
  assign driver_44_out[10] = driver_236_out ? driver_339_out : 1'bz;  // Driver driver_370
  assign driver_44_out[11] = driver_256_out ? driver_339_out : 1'bz;  // Driver driver_371
  assign driver_44_out[12] = driver_293_out ? driver_339_out : 1'bz;  // Driver driver_372
  assign driver_44_out[13] = driver_315_out ? driver_339_out : 1'bz;  // Driver driver_373
  assign driver_44_out[14] = driver_320_out ? driver_339_out : 1'bz;  // Driver driver_374
  assign driver_44_out[15] = driver_340_out ? driver_339_out : 1'bz;  // Driver driver_375
  assign driver_376_out = decoder_1_out_1 ? Conf[15] : 1'bz;  // Driver driver_376
  assign driver_377_out = and_2_out ? driver_29_out : 1'bz;  // Driver driver_377
  PullDown pulldown_37 (.out(driver_377_out));
  assign driver_377_out = and_3_out ? driver_31_out : 1'bz;  // Driver driver_378
  assign driver_44_out[7] = multiplexer_8_out ? driver_339_out : 1'bz;  // Driver driver_379
  Multiplexer multiplexer_9 (.sel(Mod), .in_0(driver_210_out), .in_1(driver_377_out), .out(multiplexer_9_out));
  Multiplexer multiplexer_10 (.sel(Mod), .in_0(b), .in_1(Cin), .out(c));
  PullDown pulldown_38 (.out(driver_376_out));
  assign driver_35_out = and_4_out ? driver_376_out : 1'bz;  // Driver driver_380
  and and_4 (and_4_out, driver_31_out, decoder_1_out_1);
  assign driver_44_out[0] = and_5_out ? driver_376_out : 1'bz;  // Driver driver_381
  and and_5 (and_5_out, multiplexer_2_out, decoder_1_out_1);
  assign driver_44_out[1] = and_6_out ? driver_376_out : 1'bz;  // Driver driver_382
  and and_6 (and_6_out, multiplexer_3_out, decoder_1_out_1);
  assign driver_44_out[2] = and_7_out ? driver_376_out : 1'bz;  // Driver driver_383
  and and_7 (and_7_out, multiplexer_4_out, decoder_1_out_1);
  assign driver_44_out[3] = and_8_out ? driver_376_out : 1'bz;  // Driver driver_384
  and and_8 (and_8_out, multiplexer_5_out, decoder_1_out_1);
  assign driver_44_out[4] = and_9_out ? driver_376_out : 1'bz;  // Driver driver_385
  and and_9 (and_9_out, multiplexer_6_out, decoder_1_out_1);
  assign driver_44_out[5] = and_10_out ? driver_376_out : 1'bz;  // Driver driver_386
  and and_10 (and_10_out, multiplexer_7_out, decoder_1_out_1);
  assign driver_44_out[6] = and_11_out ? driver_376_out : 1'bz;  // Driver driver_387
  and and_11 (and_11_out, multiplexer_8_out, decoder_1_out_1);
  assign driver_44_out[7] = and_12_out ? driver_376_out : 1'bz;  // Driver driver_388
  and and_12 (and_12_out, multiplexer_9_out, decoder_1_out_1);
  assign driver_44_out[8] = and_13_out ? driver_376_out : 1'bz;  // Driver driver_389
  and and_13 (and_13_out, driver_231_out, decoder_1_out_1);
  assign driver_44_out[9] = and_14_out ? driver_376_out : 1'bz;  // Driver driver_390
  and and_14 (and_14_out, driver_236_out, decoder_1_out_1);
  assign driver_44_out[10] = and_15_out ? driver_376_out : 1'bz;  // Driver driver_391
  and and_15 (and_15_out, driver_256_out, decoder_1_out_1);
  assign driver_44_out[11] = and_16_out ? driver_376_out : 1'bz;  // Driver driver_392
  and and_16 (and_16_out, driver_293_out, decoder_1_out_1);
  assign driver_44_out[12] = and_17_out ? driver_376_out : 1'bz;  // Driver driver_393
  and and_17 (and_17_out, driver_315_out, decoder_1_out_1);
  assign driver_44_out[13] = and_18_out ? driver_376_out : 1'bz;  // Driver driver_394
  and and_18 (and_18_out, driver_320_out, decoder_1_out_1);
  assign driver_44_out[14] = and_19_out ? driver_376_out : 1'bz;  // Driver driver_395
  and and_19 (and_19_out, driver_340_out, decoder_1_out_1);
  assign driver_44_out[15] = and_20_out ? driver_376_out : 1'bz;  // Driver driver_396
  and and_20 (and_20_out, driver_377_out, decoder_1_out_1);
  Multiplexer #(.Bits(16)) multiplexer_11 (
    .sel(ShiftBits), .in_0(Out), .in_1({Out[7:0], {8{1'b0}}}), .out({Conf[15:8], b, Conf[6:0]}));
  PullDown #(.Bits(16)) pulldown_39 (.out({driver_44_out[0], driver_44_out[1], driver_44_out[2], driver_44_out[3], driver_44_out[4], driver_44_out[5], driver_44_out[6], driver_44_out[7], driver_44_out[8], driver_44_out[9], driver_44_out[10], driver_44_out[11], driver_44_out[12], driver_44_out[13], driver_44_out[14], driver_44_out[15]}));
  PullDown #(.Bits(16)) pulldown_40 (.out(driver_44_out));
  Multiplexer #(.Bits(16)) multiplexer_12 (
    .sel(L_R),
    .in_0({driver_44_out[0], driver_44_out[1], driver_44_out[2], driver_44_out[3], driver_44_out[4], driver_44_out[5], driver_44_out[6], driver_44_out[7], driver_44_out[8], driver_44_out[9], driver_44_out[10], driver_44_out[11], driver_44_out[12], driver_44_out[13], driver_44_out[14], driver_44_out[15]}),
    .in_1(driver_44_out), .out({multiplexer_12_out, Out2[0]}));
  // Not not_4 has open pins: in=pulldown_41_out[2], out=open
  PullDown #(.Bits(4)) pulldown_41 (.out(pulldown_41_out));
  and and_21 (and_21_out, pulldown_41_out[0], pulldown_41_out[1]);
  and and_22 (and_22_out, pulldown_41_out[1], pulldown_41_out[2]);
  and and_23 (and_23_out, pulldown_41_out[0], pulldown_41_out[2]);
  and and_24 (and_24_out, pulldown_41_out[0], pulldown_41_out[1], pulldown_41_out[2]);
  and and_25 (and_25_out, pulldown_41_out[2], pulldown_41_out[3]);
  and and_26 (and_26_out, pulldown_41_out[0], pulldown_41_out[3]);
  and and_27 (and_27_out, pulldown_41_out[1], pulldown_41_out[3]);
  and and_28 (and_28_out, pulldown_41_out[0], pulldown_41_out[1], pulldown_41_out[3]);
  and and_29 (and_29_out, pulldown_41_out[0], pulldown_41_out[2], pulldown_41_out[3]);
  and and_30 (and_30_out, pulldown_41_out[1], pulldown_41_out[2], pulldown_41_out[3]);
  Multiplexer #(.Bits(16)) multiplexer_13 (.sel(ShiftBits), .in_0(Out2), .in_1({{8{1'b0}}, Out2[15:8]}), .out(Conf2));
  assign pulldown_41_out = AE ? SHC : 4'bz;  // Driver driver_397
  or or_1 (or_1_out, pulldown_41_out[0], pulldown_41_out[1], pulldown_41_out[2], pulldown_41_out[3]);
  or or_2 (or_2_out, pulldown_41_out[1], pulldown_41_out[2], pulldown_41_out[3]);
  or or_3 (or_3_out, and_21_out, pulldown_41_out[2], pulldown_41_out[3]);
  or or_4 (or_4_out, pulldown_41_out[2], pulldown_41_out[3]);
  or or_5 (or_5_out, and_22_out, and_23_out, pulldown_41_out[3]);
  or or_6 (or_6_out, and_22_out, pulldown_41_out[3]);
  or or_7 (or_7_out, and_24_out, pulldown_41_out[3]);
  or or_8 (or_8_out, and_25_out, and_26_out, and_27_out);
  or or_9 (or_9_out, and_25_out, and_27_out);
  or or_10 (or_10_out, and_25_out, and_28_out);
  or or_11 (or_11_out, and_29_out, and_30_out);
  and and_31 (and_31_out, and_30_out, pulldown_41_out[0]);
  assign CO = CE ? driver_35_out : 1'bz;  // Driver driver_398
  Multiplexer multiplexer_14 (.sel(or_1_out), .in_0(multiplexer_12_out[15]), .in_1(driver_33_out), .out(Out2[15]));
  Multiplexer multiplexer_15 (.sel(or_2_out), .in_0(multiplexer_12_out[14]), .in_1(driver_33_out), .out(Out2[14]));
  Multiplexer multiplexer_16 (.sel(or_3_out), .in_0(multiplexer_12_out[13]), .in_1(driver_33_out), .out(Out2[13]));
  Multiplexer multiplexer_17 (.sel(or_4_out), .in_0(multiplexer_12_out[12]), .in_1(driver_33_out), .out(Out2[12]));
  Multiplexer multiplexer_18 (.sel(or_5_out), .in_0(multiplexer_12_out[11]), .in_1(driver_33_out), .out(Out2[11]));
  Multiplexer multiplexer_19 (.sel(or_6_out), .in_0(multiplexer_12_out[10]), .in_1(driver_33_out), .out(Out2[10]));
  Multiplexer multiplexer_20 (.sel(or_7_out), .in_0(multiplexer_12_out[9]), .in_1(driver_33_out), .out(Out2[9]));
  Multiplexer multiplexer_21 (
    .sel(pulldown_41_out[3]), .in_0(multiplexer_12_out[8]), .in_1(driver_33_out), .out(Out2[8]));
  Multiplexer multiplexer_22 (.sel(or_8_out), .in_0(multiplexer_12_out[7]), .in_1(driver_33_out), .out(Out2[7]));
  Multiplexer multiplexer_23 (.sel(or_9_out), .in_0(multiplexer_12_out[6]), .in_1(driver_33_out), .out(Out2[6]));
  Multiplexer multiplexer_24 (.sel(or_10_out), .in_0(multiplexer_12_out[5]), .in_1(driver_33_out), .out(Out2[5]));
  Multiplexer multiplexer_25 (.sel(and_25_out), .in_0(multiplexer_12_out[4]), .in_1(driver_33_out), .out(Out2[4]));
  Multiplexer multiplexer_26 (.sel(or_11_out), .in_0(multiplexer_12_out[3]), .in_1(driver_33_out), .out(Out2[3]));
  Multiplexer multiplexer_27 (.sel(and_30_out), .in_0(multiplexer_12_out[2]), .in_1(driver_33_out), .out(Out2[2]));
  Multiplexer multiplexer_28 (.sel(and_31_out), .in_0(multiplexer_12_out[1]), .in_1(driver_33_out), .out(Out2[1]));
  PullDown pulldown_42 (.out(CO));
  assign Q = CE ? Conf2 : 16'bz;  // Driver driver_399

  // Other names for the same wires on the sheet: a = Cin; Conf[7] = b; d_t = Mod

  // Notes on the sheet:
  //   BRE: Barrel Enable
  //   L_R: Left/Right Shift
  //   0 - Left
  //   1 - Right
  //   CE: Chip Enable
  //   SHC: Shift Count
  //   0 - No Shifting
  //   ....
  //   15 - Shift 15 bits
  //   RCE: Rotate with Carry Enable
  //   CO: Carry Out
  //   Cin: Carry In
  //   AE: Arithmetic Shift Enable
  //   (Unstable with other types of shift other than ASR)
  //   Mod: Mode of Operation:
  //   1 - 8-bit values
  //   0 - 16-bit values
  //   Teoretic Shift 16, dar nu exista
endmodule
