// Digital circuit 16-bit GP-AR.dig as structural Verilog
module _16_bit_GP_AR (
  input  Clr,
  input  L,
  input  DN,
  input  UP,
  input  [15:0] D,
  input  Out,
  input  Clk,
  output [15:0] Q
);

  wire _74193_1_pin12, _74193_1_pin13, _74193_2_pin12, _74193_2_pin13, _74193_3_pin12, _74193_3_pin13,
       BorrowOut, CarryOut, Down, driver_1_out, Up_t, XLoad;
  wire [3:0] _74193_1_pin7, _74193_3_pin7, _74193_4_pin7;
  wire [7:4] _74193_2_pin7;

  assign driver_1_out = Clk ? L : 1'bz;  // Driver driver_1
  assign Down = Clk ? DN : 1'bz;  // Driver driver_2
  assign Up_t = Clk ? UP : 1'bz;  // Driver driver_3
  _74193 _74193_1 (
    .pin1(D[1]), .pin2(_74193_1_pin7[1]), .pin3(_74193_1_pin7[0]), .pin4(Down), .pin5(Up_t),
    .pin6(_74193_1_pin7[2]), .pin7(_74193_1_pin7[3]), .pin8(1'b0), .pin9(D[3]), .pin10(D[2]), .pin11(XLoad),
    .pin12(_74193_1_pin12), .pin13(_74193_1_pin13), .pin14(Clr), .pin15(D[0]), .pin16(1'b1));
  PullDown pulldown_1 (.out(driver_1_out));
  PullUp pullup_1 (.out(Down));
  not not_1 (XLoad, driver_1_out);
  PullUp pullup_2 (.out(Up_t));
  _74193 _74193_2 (
    .pin1(D[5]), .pin2(_74193_2_pin7[5]), .pin3(_74193_2_pin7[4]), .pin4(_74193_1_pin13),
    .pin5(_74193_1_pin12), .pin6(_74193_2_pin7[6]), .pin7(_74193_2_pin7[7]), .pin8(1'b0), .pin9(D[7]),
    .pin10(D[6]), .pin11(XLoad), .pin12(_74193_2_pin12), .pin13(_74193_2_pin13), .pin14(Clr), .pin15(D[4]),
    .pin16(1'b1));
  _74193 _74193_3 (
    .pin1(D[9]), .pin2(_74193_3_pin7[1]), .pin3(_74193_3_pin7[0]), .pin4(_74193_2_pin13),
    .pin5(_74193_2_pin12), .pin6(_74193_3_pin7[2]), .pin7(_74193_3_pin7[3]), .pin8(1'b0), .pin9(D[11]),
    .pin10(D[10]), .pin11(XLoad), .pin12(_74193_3_pin12), .pin13(_74193_3_pin13), .pin14(Clr), .pin15(D[8]),
    .pin16(1'b1));
  _74193 _74193_4 (
    .pin1(D[13]), .pin2(_74193_4_pin7[1]), .pin3(_74193_4_pin7[0]), .pin4(_74193_3_pin13),
    .pin5(_74193_3_pin12), .pin6(_74193_4_pin7[2]), .pin7(_74193_4_pin7[3]), .pin8(1'b0), .pin9(D[15]),
    .pin10(D[14]), .pin11(XLoad), .pin12(CarryOut), .pin13(BorrowOut), .pin14(Clr), .pin15(D[12]),
    .pin16(1'b1));
  assign Q = Out ? {_74193_4_pin7, _74193_3_pin7, _74193_2_pin7, _74193_1_pin7} : 16'bz;  // Driver driver_4

  // Other names for the same wires on the sheet: Clear = Clr; DataIN[15:0] = D; DatOUT[15:0] = Q; Output = Out

  // Notes on the sheet:
  //   Clr: Clear contents of AR
  //   L: Load value into AR (stops increments and decrements in the meanwhile)
  //   DN: Decrement the AR value
  //   UP: Increment the AR value
  //   D: Data pin (16 bits)
  //   Q: Data out (16 bits)
  //   Out: Output contents of AR
endmodule
