// Digital circuit 16-bit GPR.dig as structural Verilog
module _16_bit_GPR (
  input  [15:0] D,
  input  clk,
  input  [3:0] OPS,
  input  [1:0] LHS,
  input  [1:0] RHS,
  input  [1:0] OES,
  output [15:0] RHQ,
  output [15:0] LHQ,
  output [15:0] DBQ,
  output CO,
  output [15:0] Q0,
  output [15:0] Q1
);

  wire and_1_out, and_2_out, and_3_out, and_6_out, and_7_out, and_8_out, and_9_out, and_10_out, and_11_out,
       and_12_out, and_13_out, and_14_out, and_15_out, c, counterpreset_1_ovf, delay_1_out, driver_1_out,
       driver_3_out, driver_4_out, driver_6_out, multiplexer_3_out, not_2_out, or_1_out, or_2_out, or_3_out,
       or_4_out;
  wire [3:0] not_1_out;
  wire [7:0] and_5_out, driver_2_out, driver_2_out_2, multiplexer_1_out, multiplexer_5_out, neg_1_out,
       neg_3_out;
  wire [15:0] and_4_out, neg_2_out, pulldown_2_out, pulldown_4_out, pulldown_5_out, pulldown_7_out;

  assign not_1_out = ~OPS;  // Not not_1, 4 bits wide
  assign driver_1_out = or_1_out ? clk : 1'bz;  // Driver driver_1
  or or_1 (or_1_out, OPS[1], and_1_out, and_2_out);
  and and_1 (and_1_out, not_1_out[3], OPS[2]);
  assign {driver_2_out_2, driver_2_out} = not_2_out ? D : 16'bz;  // Driver driver_2
  Edge_Trigger_Circuit edge_trigger_circuit_1 (.In(driver_1_out), .Q(c));
  and and_2 (and_2_out, not_1_out[2], not_1_out[1], OPS[0]);
  not not_2 (not_2_out, OPS[3]);
  Delay delay_1 (.in(OPS[3]), .out(delay_1_out));
  and and_3 (and_3_out, OPS[3], OPS[2]);
  assign and_4_out = Q0 & 16'hff;  // And and_4, 16 bits wide
  assign {pulldown_2_out[7:0], and_5_out} = Q0 & 16'hff00;  // And and_5, 16 bits wide
  PullDown pulldown_1 (.out(driver_1_out));
  assign driver_3_out = or_3_out ? or_2_out : 1'bz;  // Driver driver_3
  or or_2 (or_2_out, and_6_out, and_7_out);
  and and_6 (and_6_out, not_1_out[3], not_1_out[1]);
  and and_7 (and_7_out, OPS[3], not_1_out[2]);
  Multiplexer #(.Bits(8)) multiplexer_1 (.sel(OPS[1]), .in_0(driver_2_out), .in_1(neg_1_out), .out(multiplexer_1_out));
  and and_8 (and_8_out, not_1_out[3], not_1_out[2]);
  PullDown #(.Bits(8)) pulldown_2 (.out(pulldown_2_out[15:8]));
  CounterPreset #(.maxValue(256), .Bits(8)) counterpreset_1 (
    .en(or_3_out), .C(driver_1_out), .dir(and_15_out), .in(multiplexer_1_out), .ld(driver_3_out), .clr(1'b0),
    .out(Q0[7:0]), .ovf(counterpreset_1_ovf));
  PullDown pulldown_3 (.out(driver_3_out));
  or or_3 (or_3_out, and_3_out, and_8_out, and_9_out, and_10_out, and_11_out);
  and and_9 (and_9_out, not_1_out[1], not_1_out[0]);
  Multiplexer #(.Selector_Bits(2), .Bits(16)) multiplexer_2 (
    .sel(RHS), .in_0(pulldown_4_out), .in_1(and_4_out), .in_2(pulldown_2_out), .in_3(Q0), .out(RHQ));
  PullDown #(.Bits(16)) pulldown_4 (.out(pulldown_4_out));
  Neg #(.Bits(8)) neg_1 (.in(Q0[7:0]), .out(neg_1_out));
  and and_10 (and_10_out, not_1_out[2], not_1_out[0]);
  and and_11 (and_11_out, OPS[3], not_1_out[1]);
  PullDown #(.Bits(16)) pulldown_5 (.out(pulldown_5_out));
  Multiplexer multiplexer_3 (.sel(and_3_out), .in_0(driver_1_out), .in_1(counterpreset_1_ovf), .out(multiplexer_3_out));
  and and_12 (and_12_out, not_1_out[1], OPS[0]);
  Multiplexer #(.Selector_Bits(2), .Bits(16)) multiplexer_4 (
    .sel(LHS), .in_0(pulldown_5_out), .in_1(and_4_out), .in_2(pulldown_2_out), .in_3(Q0), .out(LHQ));
  PullDown #(.Bits(16)) pulldown_6 (.out({driver_2_out_2, driver_2_out}));
  Multiplexer #(.Bits(8)) multiplexer_5 (
    .sel(OPS[1]), .in_0(driver_2_out_2), .in_1(neg_3_out), .out(multiplexer_5_out));
  assign driver_4_out = or_2_out ? or_4_out : 1'bz;  // Driver driver_4
  or or_4 (or_4_out, and_12_out, and_13_out, and_14_out);
  and and_13 (and_13_out, OPS[3], OPS[0]);
  PullDown #(.Bits(16)) pulldown_7 (.out(pulldown_7_out));
  assign {driver_2_out_2, driver_2_out} = delay_1_out ? neg_2_out : 16'bz;  // Driver driver_5
  CounterPreset #(.maxValue(256), .Bits(8)) counterpreset_2 (
    .en(or_4_out), .C(driver_6_out), .dir(and_15_out), .in(multiplexer_5_out), .ld(driver_4_out), .clr(1'b0),
    .out(Q0[15:8]), .ovf(CO));
  assign driver_6_out = c ? multiplexer_3_out : 1'bz;  // Driver driver_6
  PullDown pulldown_8 (.out(driver_4_out));
  and and_14 (and_14_out, OPS[2], OPS[1]);
  and and_15 (and_15_out, OPS[1], OPS[0]);
  Multiplexer #(.Selector_Bits(2), .Bits(16)) multiplexer_6 (
    .sel(OES), .in_0(pulldown_7_out), .in_1(and_4_out), .in_2(pulldown_2_out), .in_3(Q0), .out(DBQ));
  Neg #(.Bits(16)) neg_2 (.in(Q0), .out(neg_2_out));
  Neg #(.Bits(8)) neg_3 (.in(Q0[15:8]), .out(neg_3_out));
  PullDown pulldown_9 (.out(driver_6_out));

  assign Q1 = Q0;

  // Notes on the sheet:
  //   D: Data In
  //   OPS: Selector Bits:
  //   0000 - NOP
  //   0001 - Load value into GPR
  //   0010 - Increment-LowByte
  //   0011 - Decrement-LowByte
  //   0100 - Load GPR-LowByte
  //   0101 - Load GPR-UpperByte
  //   0110 - Increment-UpperByte
  //   0111 - Decrement-UpperByte
  //   1000 - NOP
  //   1001 - C2Invert GPR
  //   1010 - C2Invert-LowByte
  //   1011 - C2Invert-UpperByte
  //   1100 - NOP
  //   1101 - NOP
  //   1110 - Increment GPR
  //   1111 - Decrement GPR
  //   LHS: Left Hand Side Output Select:
  //   00 - NOP
  //   01 - Lower byte of GPR
  //   10 - Upper byte of GPR
  //   11 - Full value of GPR
  //   RHS: Right Hand Side Output Select:
  //   00 - NOP
  //   01 - Lower byte of GPR
  //   10 - Upper byte of GPR
  //   11 - Full value of GPR
  //   OES: Output Select:
  //   00 - NOP
  //   01 - Lower byte of GPR
  //   10 - Upper byte of GPR
  //   11 - Full value of GPR
  //   RHQ: Data out on the RHS Bus
  //   LHQ: Data out on the LHS Bus
  //   DBQ: Output for the Data Bus
  //   CO: Carry Out
  //   Q0: Output
  //   Q1: Output for the Data Bus
endmodule
