// Digital circuit Carry-RHS Decoder.dig as structural Verilog
module Carry_RHS_Decoder (
  input  [4:0] II,
  output [1:0] CSO,
  output [1:0] BSO,
  output XCE,
  output BSFR
);

  wire and_3_out, and_4_out, and_5_out, and_6_out, and_7_out, and_8_out, and_9_out, and_10_out, and_11_out,
       not_1_out, not_2_out, not_3_out, not_4_out;

  not not_1 (not_1_out, II[3]);
  not not_2 (not_2_out, II[2]);
  not not_3 (not_3_out, II[1]);
  not not_4 (not_4_out, II[0]);
  and and_1 (BSFR, II[4], not_2_out, II[1], not_4_out);
  and and_2 (CSO[0], not_1_out, II[0]);
  and and_3 (and_3_out, II[3], II[2]);
  and and_4 (and_4_out, II[3], II[0]);
  and and_5 (and_5_out, not_2_out, II[0]);
  and and_6 (and_6_out, not_1_out, not_3_out, not_4_out);
  and and_7 (and_7_out, not_2_out, not_3_out, not_4_out);
  and and_8 (and_8_out, II[3], II[1], not_4_out);
  and and_9 (and_9_out, II[1], II[2]);
  and and_10 (and_10_out, II[0], II[1]);
  and and_11 (and_11_out, II[3], II[2], II[1], II[0]);
  and and_12 (XCE, II[0], not_1_out, II[1]);
  or or_1 (CSO[1], and_3_out, and_4_out);
  or or_2 (BSO[0], and_5_out, and_6_out, and_11_out, and_7_out, and_8_out);
  or or_3 (BSO[1], and_9_out, and_10_out);

  // Notes on the sheet:
  //   CSO: Carry Select Out
  //   BSO: RHS Select Out
  //   XCE: Inverse Carry Enable
  //   BSFR: Bit Scan Forward/Backward Enable
endmodule
