// Digital circuit Clock Module.dig as structural Verilog
module Clock_Module (
  input  RST,
  input  Mode,
  input  CLK,
  input  CLKA,
  output SYNCLK,
  output SYNRST
);

  wire d_ff_1_q, d_ff_as_1_q, d_ff_as_2_q, d_ff_as_3_q, not_1_out;

  D_FF_AS d_ff_as_1 (.Set(1'b0), .D(1'b1), .C(SYNCLK), .Clr(RST), .Q(d_ff_as_1_q));  // open: nQ
  Multiplexer multiplexer_1 (.sel(d_ff_1_q), .in_0(CLK), .in_1(CLKA), .out(SYNCLK));
  not not_1 (not_1_out, d_ff_1_q);
  D_FF d_ff_1 (.D(not_1_out), .C(Mode), .Q(d_ff_1_q));  // open: nQ
  D_FF_AS d_ff_as_2 (.Set(1'b0), .D(d_ff_as_1_q), .C(SYNCLK), .Clr(RST), .Q(d_ff_as_2_q));  // open: nQ
  D_FF_AS d_ff_as_3 (.Set(1'b0), .D(d_ff_as_2_q), .C(SYNCLK), .Clr(RST), .Q(d_ff_as_3_q));  // open: nQ
  D_FF_AS d_ff_as_4 (.Set(1'b0), .D(d_ff_as_3_q), .C(SYNCLK), .Clr(RST), .Q(SYNRST));  // open: nQ

  // Notes on the sheet:
  //   Mode: Single-Step Mode/Full Speed Mode
  //   SYNCLK: Synchronized Clock
  //   SYNRST: Synchronized Reset (Active LOW)
  //   CLKA: Automated Clock
endmodule
