// Digital circuit Edge-Trigger Circuit.dig as structural Verilog
module Edge_Trigger_Circuit (
  input  In,
  output Q
);

  wire not_1_out;

  not not_1 (not_1_out, In);
  and and_1 (Q, In, not_1_out);
endmodule
