// Digital circuit Extra-Byte-Decoder.dig as structural Verilog
module Extra_Byte_Decoder (
  input  [7:0] IQ0,
  output XEN
);

  wire and_1_out, and_2_out, and_3_out, and_4_out, and_5_out, and_6_out, and_7_out, and_8_out, and_9_out,
       and_10_out, and_11_out, and_12_out, and_13_out, and_14_out, and_15_out, and_16_out, and_17_out;
  wire [7:0] not_1_out;

  assign not_1_out = ~IQ0;  // Not not_1, 8 bits wide
  and and_1 (and_1_out, not_1_out[7], not_1_out[6], not_1_out[2]);
  and and_2 (and_2_out, not_1_out[7], IQ0[5], not_1_out[3], not_1_out[2], IQ0[1]);
  and and_3 (and_3_out, not_1_out[7], IQ0[5], IQ0[3], not_1_out[2], IQ0[0]);
  and and_4 (and_4_out, not_1_out[7], IQ0[6], IQ0[4], IQ0[3]);
  and and_5 (and_5_out, IQ0[7], IQ0[6], not_1_out[5], not_1_out[2], not_1_out[1], not_1_out[0]);
  and and_6 (and_6_out, IQ0[7], IQ0[6], not_1_out[5], not_1_out[3], not_1_out[2], not_1_out[1]);
  and and_7 (and_7_out, IQ0[7], IQ0[6], not_1_out[5], IQ0[4], not_1_out[3], not_1_out[2]);
  and and_8 (and_8_out, IQ0[7], IQ0[6], not_1_out[5], IQ0[3], not_1_out[2], IQ0[1], not_1_out[0]);
  and and_9 (and_9_out, IQ0[7], IQ0[6], not_1_out[5], not_1_out[3], not_1_out[2], IQ0[1], not_1_out[0]);
  and and_10 (and_10_out, IQ0[7], IQ0[6], not_1_out[5], not_1_out[4], not_1_out[3], IQ0[2]);
  and and_11 (and_11_out, IQ0[7], IQ0[6], IQ0[5], not_1_out[4], not_1_out[2]);
  and and_12 (and_12_out, IQ0[7], not_1_out[6], IQ0[5], not_1_out[3], not_1_out[2]);
  and and_13 (and_13_out, IQ0[7], not_1_out[6], IQ0[5], IQ0[3], not_1_out[2], not_1_out[1]);
  and and_14 (and_14_out, IQ0[7], not_1_out[6], IQ0[5], IQ0[4]);
  and and_15 (and_15_out, IQ0[7], not_1_out[6], not_1_out[5], not_1_out[4]);
  and and_16 (and_16_out, not_1_out[6], not_1_out[5], IQ0[3], not_1_out[2], IQ0[1], not_1_out[0]);
  and and_17 (and_17_out, not_1_out[7], not_1_out[6], not_1_out[5], not_1_out[4], IQ0[3], IQ0[2], IQ0[1], IQ0[0]);
  or or_1 (XEN, and_1_out, and_2_out, and_3_out, and_4_out, and_5_out, and_6_out, and_7_out, and_8_out, and_9_out, and_10_out, and_11_out, and_12_out, and_13_out, and_14_out, and_15_out, and_16_out, and_17_out);

  // Notes on the sheet:
  //   IQ0: Instruction Queue 0 Input
  //   XEN: Extra Instruction Byte Enable
endmodule
