// Digital circuit Flags Register.dig as structural Verilog
module Flags_Register (
  input  [3:0] FS,
  input  L,
  input  [7:0] D,
  input  [3:0] FJS,
  output [7:0] Q,
  output INTA,
  output DIR,
  output RES
);

  wire and_1_out, and_2_out, d_ff_as_2_nq, d_ff_as_3_nq, d_ff_as_4_nq, d_ff_as_5_nq, d_ff_as_6_nq, or_1_out,
       or_2_out, xnor_1_out, xor_1_out;
  wire [7:0] decoder_1_out_0, demultiplexer_1_out_0, demultiplexer_1_out_1;

  Decoder #(.Selector_Bits(3)) decoder_1 (
    .sel(FS[3:1]), .out_0(decoder_1_out_0[0]), .out_1(decoder_1_out_0[1]), .out_2(decoder_1_out_0[2]),
    .out_3(decoder_1_out_0[3]), .out_4(decoder_1_out_0[4]), .out_5(decoder_1_out_0[5]),
    .out_6(decoder_1_out_0[6]), .out_7(decoder_1_out_0[7]));
  Demultiplexer #(.Bits(8)) demultiplexer_1 (
    .sel(FS[0]), .in(decoder_1_out_0), .out_0(demultiplexer_1_out_0), .out_1(demultiplexer_1_out_1));
  D_FF_AS d_ff_as_1 (
    .Set(demultiplexer_1_out_0[0]), .D(D[0]), .C(L), .Clr(demultiplexer_1_out_1[0]), .Q(Q[0]));  // open: nQ
  D_FF_AS d_ff_as_2 (
    .Set(demultiplexer_1_out_0[1]), .D(D[1]), .C(L), .Clr(demultiplexer_1_out_1[1]), .Q(Q[1]),
    .nQ(d_ff_as_2_nq));
  D_FF_AS d_ff_as_3 (
    .Set(demultiplexer_1_out_0[2]), .D(D[2]), .C(L), .Clr(demultiplexer_1_out_1[2]), .Q(Q[2]),
    .nQ(d_ff_as_3_nq));
  D_FF_AS d_ff_as_4 (
    .Set(demultiplexer_1_out_0[3]), .D(D[3]), .C(L), .Clr(demultiplexer_1_out_1[3]), .Q(Q[3]),
    .nQ(d_ff_as_4_nq));
  D_FF_AS d_ff_as_5 (
    .Set(demultiplexer_1_out_0[4]), .D(D[4]), .C(L), .Clr(demultiplexer_1_out_1[4]), .Q(Q[4]),
    .nQ(d_ff_as_5_nq));
  D_FF_AS d_ff_as_6 (
    .Set(demultiplexer_1_out_0[5]), .D(D[5]), .C(L), .Clr(demultiplexer_1_out_1[5]), .Q(Q[5]),
    .nQ(d_ff_as_6_nq));
  D_FF_AS d_ff_as_7 (
    .Set(demultiplexer_1_out_0[6]), .D(D[6]), .C(L), .Clr(demultiplexer_1_out_1[6]), .Q(DIR));  // open: nQ
  D_FF_AS d_ff_as_8 (
    .Set(demultiplexer_1_out_0[7]), .D(D[7]), .C(L), .Clr(demultiplexer_1_out_1[7]), .Q(INTA));  // open: nQ
  or or_1 (or_1_out, Q[1], Q[3]);
  and and_1 (and_1_out, d_ff_as_2_nq, d_ff_as_4_nq);
  xor xor_1 (xor_1_out, Q[4], Q[2]);
  xnor xnor_1 (xnor_1_out, Q[4], Q[2]);
  or or_2 (or_2_out, xor_1_out, Q[3]);
  and and_2 (and_2_out, xnor_1_out, d_ff_as_4_nq);
  Multiplexer #(.Selector_Bits(4)) multiplexer_1 (
    .sel(FJS), .in_0(Q[5]), .in_1(d_ff_as_6_nq), .in_2(Q[4]), .in_3(d_ff_as_5_nq), .in_4(Q[3]),
    .in_5(d_ff_as_4_nq), .in_6(Q[2]), .in_7(d_ff_as_3_nq), .in_8(Q[1]), .in_9(d_ff_as_2_nq),
    .in_10(or_1_out), .in_11(and_1_out), .in_12(xor_1_out), .in_13(xnor_1_out), .in_14(or_2_out),
    .in_15(and_2_out), .out(RES));

  assign Q[7:6] = {INTA, DIR};

  // Notes on the sheet:
  //   FS: Flag Operation Select
  //   Mode Bit [0]:
  //   0 - Set
  //   1 - Reset
  //   Flag Select[1-3]:
  //   000 - none
  //   001 - Carry
  //   010 - Overflow
  //   011 - Zero
  //   100 - Sign
  //   101 - Parity
  //   110 - Direction
  //   111 - Interrupt
  //   L: Flag Register Write/Latch Data
  //   D: Flag Data In
  //   Q: Flags Data Out
  //   FJS: Flag Jump Select:
  //   00000 - JP
  //   00001 - JNP
  //   00010 - JS
  //   00011 - JNS
  //   00100 - JZ
  //   00101 - JNZ
  //   00110 - JO
  //   00111 - JNO
  //   01000 - JC/JNAE/JB
  //   01001 - JNC/JAE/JNB
  //   01010 - JBE/JNA
  //   01011 - JNBE/JA
  //   01100 - JL/JNGE
  //   01101 - JNL/JGE
  //   01110 - JLE/JNG
  //   01111 - JNLE/JG
  //   INTA: Interrupt Allow
  //   0 - Do not Allow
  //   1 - Allow
  //   DIR: Direction of String Instructions
  //   0 - Increment SI/DI
  //   1 - Decrement SI/DI
  //   RES: Result of Flag Filtering
  //   N
  //   C
  //   O
  //   Z
  //   S
  //   P
  //   D
  //   I
endmodule
