// Digital circuit Instruction Queue.dig as structural Verilog
module Instruction_Queue (
  input  [7:0] D,
  input  EN,
  input  FL,
  output [7:0] Q0,
  output [7:0] Q1
);

  wire and_1_out, and_2_out, delay_1_out, not_1_out, not_2_out, not_3_out, rs_ff_as_1_q;
  wire [2:0] counter_1_out;
  wire [7:0] d_ff_1_q, d_ff_2_q, d_ff_3_q, d_ff_4_q, d_ff_5_q;

  not not_1 (not_1_out, EN);
  D_FF #(.Bits(8)) d_ff_1 (.D(D), .C(EN), .Q(d_ff_1_q));  // open: nQ
  RS_FF_AS rs_ff_as_1 (.S(FL), .R(and_2_out), .Q(rs_ff_as_1_q));  // open: nQ
  D_FF #(.Bits(8)) d_ff_2 (.D(d_ff_1_q), .C(EN), .Q(d_ff_2_q));  // open: nQ
  and and_1 (and_1_out, rs_ff_as_1_q, not_1_out);
  Delay delay_1 (.in(not_1_out), .out(delay_1_out));
  not not_2 (not_2_out, rs_ff_as_1_q);
  D_FF #(.Bits(8)) d_ff_3 (.D(d_ff_2_q), .C(EN), .Q(d_ff_3_q));  // open: nQ
  Counter #(.Bits(3)) counter_1 (.en(and_1_out), .C(delay_1_out), .clr(and_2_out), .out(counter_1_out));  // open: ovf
  D_FF #(.Bits(8)) d_ff_4 (.D(d_ff_3_q), .C(EN), .Q(d_ff_4_q));  // open: nQ
  not not_3 (not_3_out, counter_1_out[1]);
  and and_2 (and_2_out, counter_1_out[0], not_3_out, counter_1_out[2]);
  D_FF #(.Bits(8)) d_ff_5 (.D(d_ff_4_q), .C(EN), .Q(d_ff_5_q));  // open: nQ
  assign Q1 = not_2_out ? d_ff_4_q : 8'bz;  // Driver driver_1
  assign Q0 = not_2_out ? d_ff_5_q : 8'bz;  // Driver driver_2

  // Notes on the sheet:
  //   D: Data In
  //   EN: Instruction Queue Enable (Toggle)
  //   FL: Flush Toggle - Flushes the data inside the Instruction Queue
endmodule
