// Digital circuit PIR.dig as structural Verilog
module PIR (
  input  [15:0] D,
  input  L,
  output [15:0] Q
);

  D_FF #(.Bits(8)) d_ff_1 (.D(D[7:0]), .C(L), .Q(Q[7:0]));  // open: nQ
  D_FF #(.Bits(8)) d_ff_2 (.D(D[15:8]), .C(L), .Q(Q[15:8]));  // open: nQ
endmodule
