// Digital circuit Pre-Fetch Pipeline.dig as structural Verilog
module Pre_Fetch_Pipeline (
  input  [7:0] IQ1,
  input  [7:0] IQ0,
  input  CLK,
  output [15:0] Q,
  output PPL,
  output IQE
);

  wire and_1_out, and_2_out, edge_trigger_circuit_1_q, edge_trigger_circuit_3_q, extra_byte_decoder_1_xen,
       not_1_out;
  wire [7:0] d_ff_2_q;

  not not_1 (not_1_out, CLK);
  Edge_Trigger_Circuit edge_trigger_circuit_1 (.In(extra_byte_decoder_1_xen), .Q(edge_trigger_circuit_1_q));
  and and_1 (and_1_out, edge_trigger_circuit_1_q, CLK);
  Edge_Trigger_Circuit edge_trigger_circuit_2 (.In(not_1_out), .Q(PPL));
  Edge_Trigger_Circuit edge_trigger_circuit_3 (.In(CLK), .Q(edge_trigger_circuit_3_q));
  D_FF #(.Bits(8)) d_ff_1 (.D(IQ0), .C(CLK), .Q(Q[7:0]));  // open: nQ
  Extra_Byte_Decoder extra_byte_decoder_1 (.IQ0(Q[7:0]), .XEN(extra_byte_decoder_1_xen));
  D_FF #(.Bits(8)) d_ff_2 (.D(IQ1), .C(and_1_out), .Q(d_ff_2_q));  // open: nQ
  and and_2 (and_2_out, extra_byte_decoder_1_xen, PPL);
  assign Q[15:8] = extra_byte_decoder_1_xen ? d_ff_2_q : 8'bz;  // Driver driver_1
  PullDown #(.Bits(8)) pulldown_1 (.out(Q[15:8]));
  or or_1 (IQE, and_2_out, edge_trigger_circuit_3_q);

  // Notes on the sheet:
  //   IQ1: Instruction Queue 0 Input
  //   IQ0: Instruction Queue 1 Input
  //   PPL: Pipeline Stage 0 Latch
  //   IQE: Instruction Queue Enable
endmodule
