// Digital circuit Program Counter.dig as structural Verilog
module Program_Counter (
  input  RST,
  input  CLK,
  input  [15:0] AAJ,
  input  [1:0] SS,
  input  [15:0] JO,
  input  [1:0] JS,
  input  CE,
  output [15:0] Q
);

  wire nand_1_out;
  wire [15:0] add_1_s, add_2_s, multiplexer_1_out, multiplexer_2_out;

  Add #(.Bits(16)) add_1 (.a(Q), .b({{14{1'b0}}, SS}), .c_i(1'b1), .s(add_1_s));  // open: c_o
  Add #(.Bits(16)) add_2 (.a(Q), .b(JO), .c_i(1'b0), .s(add_2_s));  // open: c_o
  Multiplexer #(.Selector_Bits(2), .Bits(16)) multiplexer_1 (
    .sel(JS), .in_0(add_1_s), .in_1(add_2_s), .in_2(AAJ), .in_3({16{1'b0}}), .out(multiplexer_1_out));
  Multiplexer #(.Bits(16)) multiplexer_2 (
    .sel(RST), .in_0({16{1'b0}}), .in_1(multiplexer_1_out), .out(multiplexer_2_out));
  nand nand_1 (nand_1_out, CE, RST);
  Register #(.Bits(16)) register_1 (.D(multiplexer_2_out), .C(CLK), .en(nand_1_out), .Q(Q));

  // Notes on the sheet:
  //   AAJ: Absolute Address Jump Input
  //   SS: Step Size
  //   00 - 1-byte step
  //   01 - 2-byte step
  //   10 - 3-byte step
  //   11 - 4-byte step
  //   JO: Jump Offset
  //   JS: Jump Select
  //   00 - NONE (Stall)
  //   01 - Single-Step
  //   10 - Relative Jump Address
  //   11 - FIxed Jump Address
  //   CE: Clock Enable
endmodule
