// Digital circuit Register Page.dig as structural Verilog
module Register_Page (
  input  [3:0] RHS,
  input  [3:0] LHS,
  input  [5:0] OPS,
  input  [15:0] D,
  input  CLK,
  input  RST,
  input  [4:0] OE,
  output [15:0] Q,
  output [15:0] LHQ,
  output [15:0] RHQ
);

  wire d_ff_1_q, decoder_1_out_0, decoder_1_out_1, decoder_1_out_2, decoder_1_out_3, decoder_1_out_4,
       decoder_1_out_5, decoder_1_out_6, decoder_1_out_7, decoder_2_out_0, decoder_2_out_1, decoder_2_out_2,
       decoder_2_out_3, decoder_3_out_0, decoder_3_out_1, decoder_3_out_2, decoder_3_out_3, decoder_3_out_4,
       decoder_3_out_5, decoder_3_out_6, decoder_3_out_7, decoder_4_out_0, decoder_4_out_1, decoder_4_out_2,
       decoder_4_out_3, edge_trigger_circuit_1_q, GPR_A_p14, GPR_B_p14, GPR_C_p14, GPR_D_p14, nor_1_out,
       not_1_out, not_2_out, not_3_out, or_1_out, or_2_out;
  wire [1:0] driver_2_out, driver_3_out, driver_7_out, driver_11_out, driver_15_out, driver_18_out,
       driver_22_out, driver_23_out, pulldown_2_out, pulldown_6_out, pulldown_10_out, pulldown_14_out;
  wire [2:0] driver_30_out, driver_31_out, driver_34_out, driver_35_out, pulldown_1_out, pulldown_5_out,
       pulldown_9_out, pulldown_13_out;
  wire [15:0] DI_2_q, DI_q, driver_1_out, GPR_A_p15, GPR_A_p16, GPR_A_p17, GPR_B_p15, GPR_B_p16, GPR_B_p17,
       GPR_C_p15, GPR_C_p16, GPR_C_p17, GPR_D_p15, GPR_D_p16, GPR_D_p17, SI_2_q, SI_q;

  PullDown #(.Bits(3)) pulldown_1 (.out(pulldown_1_out));
  PullDown #(.Bits(2)) pulldown_2 (.out(pulldown_2_out));
  nor nor_1 (nor_1_out, OE[0], OE[1], OE[2], OE[3], OE[4]);
  assign driver_1_out = nor_1_out ? D : 16'bz;  // Driver driver_1
  Decoder #(.Selector_Bits(3)) decoder_1 (
    .sel(OE[4:2]), .out_0(decoder_1_out_0), .out_1(decoder_1_out_1), .out_2(decoder_1_out_2),
    .out_3(decoder_1_out_3), .out_4(decoder_1_out_4), .out_5(decoder_1_out_5), .out_6(decoder_1_out_6),
    .out_7(decoder_1_out_7));
  or or_1 (or_1_out, OE[4], OE[3], OE[2], OE[1], OE[0]);
  Decoder #(.Selector_Bits(2)) decoder_2 (
    .sel(RHS[3:2]), .out_0(decoder_2_out_0), .out_1(decoder_2_out_1), .out_2(decoder_2_out_2),
    .out_3(decoder_2_out_3));
  Decoder #(.Selector_Bits(3)) decoder_3 (
    .sel(OPS[5:3]), .out_0(decoder_3_out_0), .out_1(decoder_3_out_1), .out_2(decoder_3_out_2),
    .out_3(decoder_3_out_3), .out_4(decoder_3_out_4), .out_5(decoder_3_out_5), .out_6(decoder_3_out_6),
    .out_7(decoder_3_out_7));
  Decoder #(.Selector_Bits(2)) decoder_4 (
    .sel(LHS[3:2]), .out_0(decoder_4_out_0), .out_1(decoder_4_out_1), .out_2(decoder_4_out_2),
    .out_3(decoder_4_out_3));
  not not_1 (not_1_out, not_2_out);
  not not_2 (not_2_out, edge_trigger_circuit_1_q);
  Edge_Trigger_Circuit edge_trigger_circuit_1 (.In(not_3_out), .Q(edge_trigger_circuit_1_q));
  not not_3 (not_3_out, CLK);
  assign driver_2_out = decoder_4_out_3 ? LHS[1:0] : 2'bz;  // Driver driver_2
  assign driver_3_out = decoder_2_out_3 ? RHS[1:0] : 2'bz;  // Driver driver_3
  PullDown #(.Bits(2)) pulldown_3 (.out(driver_3_out));
  PullDown #(.Bits(2)) pulldown_4 (.out(driver_2_out));
  assign pulldown_1_out = decoder_3_out_3 ? OPS[2:0] : 3'bz;  // Driver driver_4
  assign pulldown_2_out = decoder_1_out_3 ? OE[1:0] : 2'bz;  // Driver driver_5
  D_FF d_ff_1 (.D(or_2_out), .C(not_1_out), .Q(d_ff_1_q));  // open: nQ
  // _16_bit_GPR GPR_D: pin names not known; wires that end beside it: d_ff_1_q, driver_1_out, pulldown_1_out[2], pulldown_1_out[1], pulldown_1_out[0], pulldown_2_out[1], pulldown_2_out[0], CLK, RST, driver_2_out[1], driver_2_out[0], driver_3_out[1], driver_3_out[0], GPR_D_p14, GPR_D_p15, GPR_D_p16, GPR_D_p17
  or or_2 (or_2_out, GPR_A_p14, GPR_B_p14, GPR_C_p14, GPR_D_p14);
  assign RHQ = decoder_2_out_3 ? GPR_D_p17 : 16'bz;  // Driver driver_6
  assign driver_7_out = decoder_2_out_2 ? RHS[1:0] : 2'bz;  // Driver driver_7
  assign driver_1_out = decoder_1_out_3 ? GPR_D_p15 : 16'bz;  // Driver driver_8
  PullDown #(.Bits(3)) pulldown_5 (.out(pulldown_5_out));
  PullDown #(.Bits(2)) pulldown_6 (.out(pulldown_6_out));
  PullDown #(.Bits(2)) pulldown_7 (.out(driver_7_out));
  assign LHQ = decoder_4_out_3 ? GPR_D_p16 : 16'bz;  // Driver driver_9
  assign pulldown_6_out = decoder_1_out_2 ? OE[1:0] : 2'bz;  // Driver driver_10
  assign driver_11_out = decoder_4_out_2 ? LHS[1:0] : 2'bz;  // Driver driver_11
  PullDown #(.Bits(2)) pulldown_8 (.out(driver_11_out));
  LED SF (.in(d_ff_1_q));
  assign pulldown_5_out = decoder_3_out_2 ? OPS[2:0] : 3'bz;  // Driver driver_12
  // _16_bit_GPR GPR_C: pin names not known; wires that end beside it: d_ff_1_q, driver_1_out, pulldown_5_out[2], pulldown_5_out[1], pulldown_5_out[0], pulldown_6_out[1], pulldown_6_out[0], CLK, RST, driver_11_out[1], driver_11_out[0], driver_7_out[1], driver_7_out[0], GPR_C_p14, GPR_C_p15, GPR_C_p16, GPR_C_p17
  assign driver_1_out = decoder_1_out_2 ? GPR_C_p15 : 16'bz;  // Driver driver_13
  assign RHQ = decoder_2_out_2 ? GPR_C_p17 : 16'bz;  // Driver driver_14
  assign driver_15_out = decoder_2_out_1 ? RHS[1:0] : 2'bz;  // Driver driver_15
  PullDown #(.Bits(3)) pulldown_9 (.out(pulldown_9_out));
  PullDown #(.Bits(2)) pulldown_10 (.out(pulldown_10_out));
  PullDown #(.Bits(2)) pulldown_11 (.out(driver_15_out));
  assign LHQ = decoder_4_out_2 ? GPR_C_p16 : 16'bz;  // Driver driver_16
  assign pulldown_10_out = decoder_1_out_1 ? OE[1:0] : 2'bz;  // Driver driver_17
  assign driver_18_out = decoder_4_out_1 ? LHS[1:0] : 2'bz;  // Driver driver_18
  PullDown #(.Bits(2)) pulldown_12 (.out(driver_18_out));
  // _16_bit_GPR GPR_B: pin names not known; wires that end beside it: d_ff_1_q, driver_1_out, pulldown_9_out[2], pulldown_9_out[1], pulldown_9_out[0], pulldown_10_out[1], pulldown_10_out[0], CLK, RST, driver_18_out[1], driver_18_out[0], driver_15_out[1], driver_15_out[0], GPR_B_p14, GPR_B_p15, GPR_B_p16, GPR_B_p17
  assign pulldown_9_out = decoder_3_out_1 ? OPS[2:0] : 3'bz;  // Driver driver_19
  assign driver_1_out = decoder_1_out_1 ? GPR_B_p15 : 16'bz;  // Driver driver_20
  assign RHQ = decoder_2_out_1 ? GPR_B_p17 : 16'bz;  // Driver driver_21
  assign driver_22_out = decoder_4_out_0 ? LHS[1:0] : 2'bz;  // Driver driver_22
  assign driver_23_out = decoder_2_out_0 ? RHS[1:0] : 2'bz;  // Driver driver_23
  PullDown #(.Bits(3)) pulldown_13 (.out(pulldown_13_out));
  PullDown #(.Bits(2)) pulldown_14 (.out(pulldown_14_out));
  PullDown #(.Bits(2)) pulldown_15 (.out(driver_23_out));
  PullDown #(.Bits(2)) pulldown_16 (.out(driver_22_out));
  assign LHQ = decoder_4_out_1 ? GPR_B_p16 : 16'bz;  // Driver driver_24
  assign pulldown_13_out = decoder_3_out_0 ? OPS[2:0] : 3'bz;  // Driver driver_25
  assign pulldown_14_out = decoder_1_out_0 ? OE[1:0] : 2'bz;  // Driver driver_26
  // _16_bit_GPR GPR_A: pin names not known; wires that end beside it: d_ff_1_q, driver_1_out, pulldown_13_out[2], pulldown_13_out[1], pulldown_13_out[0], pulldown_14_out[1], pulldown_14_out[0], CLK, RST, driver_22_out[1], driver_22_out[0], driver_23_out[1], driver_23_out[0], GPR_A_p14, GPR_A_p15, GPR_A_p16, GPR_A_p17
  assign driver_1_out = decoder_1_out_0 ? GPR_A_p15 : 16'bz;  // Driver driver_27
  assign LHQ = decoder_4_out_0 ? GPR_A_p16 : 16'bz;  // Driver driver_28
  assign RHQ = decoder_2_out_0 ? GPR_A_p17 : 16'bz;  // Driver driver_29
  assign driver_30_out = decoder_3_out_6 ? OPS[2:0] : 3'bz;  // Driver driver_30
  assign driver_31_out = decoder_3_out_7 ? OPS[2:0] : 3'bz;  // Driver driver_31
  _16_bit_GP_AR DI (
    .D(driver_1_out), .L(driver_31_out[2]), .DN(driver_31_out[1]), .UP(driver_31_out[0]),
    .Out(decoder_1_out_7), .Clr(RST), .Clk(CLK), .Q(DI_q));
  _16_bit_GP_AR SI (
    .D(driver_1_out), .L(driver_30_out[2]), .DN(driver_30_out[1]), .UP(driver_30_out[0]),
    .Out(decoder_1_out_6), .Clr(RST), .Clk(CLK), .Q(SI_q));
  assign driver_1_out = decoder_1_out_7 ? DI_q : 16'bz;  // Driver driver_32
  assign driver_1_out = decoder_1_out_6 ? SI_q : 16'bz;  // Driver driver_33
  assign driver_34_out = decoder_3_out_4 ? OPS[2:0] : 3'bz;  // Driver driver_34
  assign driver_35_out = decoder_3_out_5 ? OPS[2:0] : 3'bz;  // Driver driver_35
  _16_bit_GP_AR DI_2 (
    .D(driver_1_out), .L(driver_35_out[2]), .DN(driver_35_out[1]), .UP(driver_35_out[0]),
    .Out(decoder_1_out_5), .Clr(RST), .Clk(CLK), .Q(DI_2_q));
  _16_bit_GP_AR SI_2 (
    .D(driver_1_out), .L(driver_34_out[2]), .DN(driver_34_out[1]), .UP(driver_34_out[0]),
    .Out(decoder_1_out_4), .Clr(RST), .Clk(CLK), .Q(SI_2_q));
  assign driver_1_out = decoder_1_out_5 ? DI_2_q : 16'bz;  // Driver driver_36
  assign driver_1_out = decoder_1_out_4 ? SI_2_q : 16'bz;  // Driver driver_37
  assign Q = or_1_out ? driver_1_out : 16'bz;  // Driver driver_38

  // Notes on the sheet:
  //   RHS: Right Hand Side Output Select
  //   Register Select bits (2-3):
  //   00 - GPR-A
  //   01 - GPR-B
  //   10 - GPR-C
  //   11 - GPR-D
  //   Section bits (0-1):
  //   00 - NOP
  //   01 - Lower byte of GPR
  //   10 - Upper byte of GPR
  //   11 - Full value of GPR
  //   LHS: Left Hand Side Output Select
  //   Register Select bits (2-3):
  //   00 - GPR-A
  //   01 - GPR-B
  //   10 - GPR-C
  //   11 - GPR-D
  //   Section bits (0-1):
  //   00 - NOP
  //   01 - Lower byte of GPR
  //   10 - Upper byte of GPR
  //   11 - Full value of GPR
  //   OPS: GPR/GP-AR Operation Select
  //   Register Select Bits (3-5):
  //   000 - GPR-A
  //   001 - GPR-B
  //   010 - GPR-C
  //   011 - GPR-D
  //   100 - SP
  //   101 - BP
  //   110 - SI
  //   111 - DI
  //   GPR Operand Bits (0-2):
  //   000 - NOP
  //   001 - Shift value of GPR to the right
  //   010 - Shift value of GPR to the left
  //   011 - Load Lower Byte of GPR
  //   100 - Load value into GPR (stops increments and decrements in the meanwhile)
  //   101 - Increment value of GPR
  //   110 - Decrement value of GPR
  //   111 - Load Upper Byte of GPR
  //   GP-AR Operand Bits (0-2):
  //   000 - NOP
  //   001 - Increment value
  //   010 - Decrement value
  //   100 - Load new value from Data Bus
  //   D: Data In
  //   OE: Output Decoder
  //   General state:
  //   00000 - Take Input from outside
  //   Register Select bits (2-4):
  //   000 - GPR-A
  //   001 - GPR-B
  //   010 - GPR-C
  //   011 - GPR-D
  //   100 - SP
  //   101 - BP
  //   110 - SI
  //   111 - DI
  //   Segment bits (0-1):
  //   00 - NOP
  //   01 - Lower Byte of GPR
  //   10 - Upper Byte of GPR
  //   11 - Full Value of GPR
endmodule
