// Digital circuit Doggo-CPU.dig as structural Verilog
module Doggo_CPU (
  input  [15:0] D,
  input  [4:0] RHS,
  input  [4:0] LHS,
  input  [4:0] OES,
  input  GPRI,
  input  [6:0] OPS,
  input  [2:0] INDS,
  input  [2:0] BAS,
  input  P0,
  input  clk,
  input  clk_2,
  input  FEN,
  input  P1,
  input  [7:0] D_2,
  input  [7:0] Flags,
  input  [15:0] A,
  input  [15:0] B,
  input  [4:0] OP,
  input  [3:0] FI,
  input  [3:0] FS,
  input  L,
  input  [7:0] D_3,
  input  [3:0] FJS,
  input  Clk_3,
  output [15:0] Q,
  output [15:0] RHQ,
  output [15:0] LHQ,
  output [15:0] BAQ,
  output [15:0] NDQ,
  output [7:0] ST_0,
  output [7:0] ST_1,
  output [7:0] ST_2,
  output [7:0] ST_3,
  output [23:0] uOP_0,
  output [23:0] uOP_1,
  output [23:0] uOP_2,
  output [15:0] Q_2,
  output [3:0] FO,
  output [7:0] Q_3,
  output INTA,
  output DIR,
  output RES
);

  wire add_1_c_o, add_2_c_o, and_1_out, and_2_out, and_8_out, and_9_out, and_10_out, and_11_out, any, bs,
       carry_rhs_decoder_1_xce, clk_t, d_ff_as_2_nq, d_ff_as_3_nq, d_ff_as_4_nq, d_ff_as_5_nq, d_ff_as_6_nq,
       delay_1_out, delay_2_out, driver_2_out, driver_17_out, driver_18_out, multiplexer_2_out,
       multiplexer_4_out, multiplexer_5_out, nor_1_out, not_1_out, not_2_out, not_4_out, not_7_out,
       not_8_out, not_9_out, not_10_out, not_11_out, not_12_out, or_4_out, or_5_out, or_6_out, or_7_out,
       or_8_out, or_9_out, or_10_out, or_11_out, or_12_out, or_13_out, or_14_out, or_15_out, or_16_out,
       or_17_out, or_18_out, or_19_out, or_20_out, or_21_out, or_22_out, or_23_out, or_24_out, or_25_out,
       or_26_out, or_27_out, or_28_out, or_29_out, or_30_out, outCarryShift, priorityencoder_1_any, xclk,
       xnor_1_out, xor_2_out;
  wire [0:0] driver_5_out;
  wire [1:0] and_6_out, and_7_out, carry_rhs_decoder_1_bso, carry_rhs_decoder_1_cso, demultiplexer_2_out_0,
       demultiplexer_2_out_1, demultiplexer_2_out_2, demultiplexer_2_out_3, demultiplexer_2_out_4,
       demultiplexer_2_out_5, demultiplexer_2_out_6, demultiplexer_3_out_0, demultiplexer_3_out_1,
       demultiplexer_3_out_2, demultiplexer_3_out_3, demultiplexer_3_out_4, demultiplexer_3_out_5,
       demultiplexer_3_out_6, demultiplexer_4_out_0, demultiplexer_4_out_1, demultiplexer_4_out_2,
       demultiplexer_4_out_3, demultiplexer_4_out_4, demultiplexer_4_out_5, demultiplexer_4_out_6,
       multiplexer_7_out;
  wire [2:0] driver_5_out_2;
  wire [3:0] demultiplexer_5_out_0, demultiplexer_5_out_1, demultiplexer_5_out_2, demultiplexer_5_out_3,
       demultiplexer_5_out_4, demultiplexer_5_out_5, demultiplexer_5_out_6, priorityencoder_1_num;
  wire [7:0] d_ff_1_q, d_ff_2_q, d_ff_3_q, d_ff_4_q, d_ff_5_q, d_ff_9_q, d_ff_10_q, d_ff_11_q, d_ff_12_q,
       d_ff_16_q, d_ff_17_q, d_ff_18_q, d_ff_19_q, decoder_1_out_7, decoder_2_out_0, decoder_3_out_0,
       demultiplexer_1_out_0, demultiplexer_1_out_1, multiplexer_1_out, multiplexer_10_out;
  wire [15:0] _16_bit_barrel_shifter_1_q, _16_bit_gpr_1_dbq, _16_bit_gpr_1_lhq, _16_bit_gpr_1_q0,
       _16_bit_gpr_1_q1, _16_bit_gpr_1_rhq, _16_bit_gpr_2_dbq, _16_bit_gpr_2_lhq, _16_bit_gpr_2_q0,
       _16_bit_gpr_2_q1, _16_bit_gpr_2_rhq, _16_bit_gpr_3_dbq, _16_bit_gpr_3_lhq, _16_bit_gpr_3_q0,
       _16_bit_gpr_3_q1, _16_bit_gpr_3_rhq, _16_bit_gpr_4_dbq, _16_bit_gpr_4_lhq, _16_bit_gpr_4_q0,
       _16_bit_gpr_4_q1, _16_bit_gpr_4_rhq, _16_bit_gpr_5_dbq, _16_bit_gpr_5_lhq, _16_bit_gpr_5_q0,
       _16_bit_gpr_5_q1, _16_bit_gpr_5_rhq, _16_bit_gpr_6_dbq, _16_bit_gpr_6_lhq, _16_bit_gpr_6_q0,
       _16_bit_gpr_6_q1, _16_bit_gpr_6_rhq, _16_bit_gpr_7_dbq, _16_bit_gpr_7_lhq, _16_bit_gpr_7_q0,
       _16_bit_gpr_7_q1, _16_bit_gpr_7_rhq, _16_bit_gpr_8_dbq, _16_bit_gpr_8_lhq, _16_bit_gpr_8_q0,
       _16_bit_gpr_8_q1, _16_bit_gpr_8_rhq, add_2_s, and_3_out, driver_1_out, multiplexer_3_out, not_3_out,
       not_6_out, or_1_out, xor_1_out;
  wire [15:8] multiplexer_1_out_2;
  wire [15:14] demultiplexer_2_out_7, demultiplexer_3_out_7, demultiplexer_4_out_7;
  wire [23:0] d_ff_6_q, d_ff_7_q, d_ff_8_q, d_ff_13_q, d_ff_14_q, d_ff_15_q, rom_1_d, rom_2_d, rom_3_d;
  wire [31:28] demultiplexer_5_out_7;

  Carry_RHS_Decoder carry_rhs_decoder_1 (
    .II(OP), .CSO(carry_rhs_decoder_1_cso), .BSO(carry_rhs_decoder_1_bso), .XCE(carry_rhs_decoder_1_xce),
    .BSFR(bs));
  not not_1 (not_1_out, OP[4]);
  not not_2 (not_2_out, OP[2]);
  Delay delay_1 (.in(OP[2]), .out(delay_1_out));
  assign not_3_out = ~B;  // Not not_3, 16 bits wide
  and and_1 (and_1_out, OP[1], not_2_out);
  and and_2 (and_2_out, delay_1_out, OP[1]);
  Multiplexer #(.Selector_Bits(2), .Bits(16)) multiplexer_1 (
    .sel(carry_rhs_decoder_1_bso), .in_0({16{1'b0}}), .in_1(B), .in_2({16{1'b1}}), .in_3(not_3_out),
    .out({multiplexer_1_out_2, multiplexer_1_out}));
  Multiplexer #(.Selector_Bits(2)) multiplexer_2 (
    .sel(carry_rhs_decoder_1_cso), .in_0(1'b0), .in_1(FI[0]), .in_2(1'b1), .in_3(FI[0]),
    .out(multiplexer_2_out));
  not not_4 (not_4_out, multiplexer_2_out);
  Multiplexer #(.Bits(16)) multiplexer_3 (
    .sel(OP[3]), .in_0(A),
    .in_1({A[0], A[1], A[2], A[3], A[4], A[5], A[6], A[7], A[8], A[9], A[10], A[11], A[12], A[13], A[14], A[15]}),
    .out(multiplexer_3_out));
  Multiplexer multiplexer_4 (
    .sel(carry_rhs_decoder_1_xce), .in_0(multiplexer_2_out), .in_1(not_4_out), .out(multiplexer_4_out));
  not not_5 (any, priorityencoder_1_any);
  PriorityEncoder #(.Selector_Bits(4)) priorityencoder_1 (
    .in0(multiplexer_3_out[0]), .in1(multiplexer_3_out[1]), .in2(multiplexer_3_out[2]),
    .in3(multiplexer_3_out[3]), .in4(multiplexer_3_out[4]), .in5(multiplexer_3_out[5]),
    .in6(multiplexer_3_out[6]), .in7(multiplexer_3_out[7]), .in8(multiplexer_3_out[8]),
    .in9(multiplexer_3_out[9]), .in10(multiplexer_3_out[10]), .in11(multiplexer_3_out[11]),
    .in12(multiplexer_3_out[12]), .in13(multiplexer_3_out[13]), .in14(multiplexer_3_out[14]),
    .in15(multiplexer_3_out[15]), .num(priorityencoder_1_num), .any(priorityencoder_1_any));
  Add #(.Bits(8)) add_1 (.a(A[7:0]), .b(multiplexer_1_out), .c_i(multiplexer_4_out), .c_o(add_1_c_o));  // open: s
  Add #(.Bits(16)) add_2 (
    .a(A), .b({multiplexer_1_out_2, multiplexer_1_out}), .c_i(multiplexer_4_out), .s(add_2_s), .c_o(add_2_c_o));
  assign and_3_out = A & {multiplexer_1_out_2, multiplexer_1_out};  // And and_3, 16 bits wide
  assign or_1_out = A | {multiplexer_1_out_2, multiplexer_1_out};  // Or or_1, 16 bits wide
  assign xor_1_out = A ^ {multiplexer_1_out_2, multiplexer_1_out};  // XOr xor_1, 16 bits wide
  assign not_6_out = ~A;  // Not not_6, 16 bits wide
  _16_bit_Barrel_Shifter _16_bit_barrel_shifter_1 (
    .D(A), .BRE(OP[2]), .L_R(OP[0]), .CE(OP[4]), .SHC(B[3:0]), .RCE(and_2_out), .Cin(FI[0]), .AE(and_1_out),
    .Mod(OP[3]), .Q(_16_bit_barrel_shifter_1_q), .CO(outCarryShift));
  assign driver_1_out = not_1_out ? add_2_s : 16'bz;  // Driver driver_1
  assign driver_2_out = not_1_out ? add_2_c_o : 1'bz;  // Driver driver_2
  assign clk_t = clk ? clk_2 : 1'bz;  // Driver driver_3
  Driver #(.invertDriverOutput("true")) driver_4 (.in(clk_2), .en(clk));  // open: out
  PullDown #(.Bits(16)) pulldown_1 (.out(driver_1_out));
  PullDown pulldown_2 (.out(clk_t));
  PullDown pulldown_3 (.out(xclk));
  not not_7 (not_7_out, driver_1_out[15]);
  and and_4 (and_6_out[1], not_7_out, A[15], B[15]);
  not not_8 (not_8_out, driver_1_out[7]);
  and and_5 (and_7_out[0], not_8_out, A[7], B[7]);
  Multiplexer multiplexer_5 (.sel(and_8_out), .in_0(driver_2_out), .in_1(add_1_c_o), .out(multiplexer_5_out));
  not not_9 (not_9_out, A[15]);
  not not_10 (not_10_out, B[15]);
  and and_6 (and_6_out[0], driver_1_out[15], not_9_out, not_10_out);
  not not_11 (not_11_out, A[7]);
  not not_12 (not_12_out, B[7]);
  and and_7 (and_7_out[1], driver_1_out[7], not_11_out, not_12_out);
  Multiplexer #(.Selector_Bits(5), .Bits(16)) multiplexer_6 (
    .sel(OP), .in_0(driver_1_out), .in_1(driver_1_out), .in_2(not_6_out), .in_3(driver_1_out),
    .in_4(xor_1_out), .in_5(driver_1_out), .in_6(driver_1_out), .in_7(driver_1_out), .in_8(and_3_out),
    .in_9(driver_1_out), .in_10(or_1_out), .in_11(driver_1_out), .in_12(driver_1_out), .in_13(driver_1_out),
    .in_14(driver_1_out), .in_15(driver_1_out), .in_16(_16_bit_barrel_shifter_1_q),
    .in_17(_16_bit_barrel_shifter_1_q), .in_18({{12{1'b0}}, priorityencoder_1_num}),
    .in_19(_16_bit_barrel_shifter_1_q), .in_20(_16_bit_barrel_shifter_1_q),
    .in_21(_16_bit_barrel_shifter_1_q), .in_22(_16_bit_barrel_shifter_1_q),
    .in_23(_16_bit_barrel_shifter_1_q), .in_24(_16_bit_barrel_shifter_1_q),
    .in_25(_16_bit_barrel_shifter_1_q), .in_26({{12{1'b0}}, priorityencoder_1_num}),
    .in_27(_16_bit_barrel_shifter_1_q), .in_28(_16_bit_barrel_shifter_1_q),
    .in_29(_16_bit_barrel_shifter_1_q), .in_30(_16_bit_barrel_shifter_1_q),
    .in_31(_16_bit_barrel_shifter_1_q), .out({FO[2], Q_2[14:0]}));
  PullDown pulldown_4 (.out(multiplexer_5_out));
  and and_8 (and_8_out, ~OP[4], OP[3], OP[2], OP[1], OP[0]);  // And
  Multiplexer #(.Bits(2)) multiplexer_7 (.sel(and_8_out), .in_0(and_6_out), .in_1(and_7_out), .out(multiplexer_7_out));
  nor nor_1 (nor_1_out, FO[2], Q_2[14], Q_2[13], Q_2[12], Q_2[11], Q_2[10], Q_2[9], Q_2[8], Q_2[7], Q_2[6], Q_2[5], Q_2[4], Q_2[3], Q_2[2], Q_2[1], Q_2[0]);
  or or_2 (FO[0], outCarryShift, multiplexer_5_out);
  Multiplexer multiplexer_8 (.sel(bs), .in_0(nor_1_out), .in_1(any), .out(FO[1]));
  or or_3 (FO[3], multiplexer_7_out[1], multiplexer_7_out[0]);
  assign {driver_5_out_2, driver_5_out[0]} = Clk_3 ? FS : 4'bz;  // Driver driver_5
  PullDown #(.Bits(4)) pulldown_5 (.out({driver_5_out_2, driver_5_out[0]}));
  Decoder #(.Selector_Bits(3)) decoder_1 (
    .sel(driver_5_out_2), .out_0(decoder_1_out_7[0]), .out_1(decoder_1_out_7[1]), .out_2(decoder_1_out_7[2]),
    .out_3(decoder_1_out_7[3]), .out_4(decoder_1_out_7[4]), .out_5(decoder_1_out_7[5]),
    .out_6(decoder_1_out_7[6]), .out_7(decoder_1_out_7[7]));
  and and_9 (and_9_out, Clk_3, L);
  assign Q = GPRI ? D : 16'bz;  // Driver driver_6
  Demultiplexer #(.Bits(8)) demultiplexer_1 (
    .sel(driver_5_out[0]), .in(decoder_1_out_7), .out_0(demultiplexer_1_out_0), .out_1(demultiplexer_1_out_1));
  D_FF_AS d_ff_as_1 (
    .Set(demultiplexer_1_out_0[0]), .D(D_3[0]), .C(and_9_out), .Clr(demultiplexer_1_out_1[0]), .Q(Q_3[0]));  // open: nQ
  D_FF_AS d_ff_as_2 (
    .Set(demultiplexer_1_out_0[1]), .D(D_3[1]), .C(and_9_out), .Clr(demultiplexer_1_out_1[1]), .Q(Q_3[1]),
    .nQ(d_ff_as_2_nq));
  Demultiplexer #(.Selector_Bits(3), .Bits(2)) demultiplexer_2 (
    .sel(OES[4:2]), .in(OES[1:0]), .out_0(demultiplexer_2_out_0), .out_1(demultiplexer_2_out_1),
    .out_2(demultiplexer_2_out_2), .out_3(demultiplexer_2_out_3), .out_4(demultiplexer_2_out_4),
    .out_5(demultiplexer_2_out_5), .out_6(demultiplexer_2_out_6), .out_7(demultiplexer_2_out_7));
  D_FF_AS d_ff_as_3 (
    .Set(demultiplexer_1_out_0[2]), .D(D_3[2]), .C(and_9_out), .Clr(demultiplexer_1_out_1[2]), .Q(Q_3[2]),
    .nQ(d_ff_as_3_nq));
  D_FF_AS d_ff_as_4 (
    .Set(demultiplexer_1_out_0[3]), .D(D_3[3]), .C(and_9_out), .Clr(demultiplexer_1_out_1[3]), .Q(Q_3[3]),
    .nQ(d_ff_as_4_nq));
  Demultiplexer #(.Selector_Bits(3), .Bits(2)) demultiplexer_3 (
    .sel(RHS[4:2]), .in(RHS[1:0]), .out_0(demultiplexer_3_out_0), .out_1(demultiplexer_3_out_1),
    .out_2(demultiplexer_3_out_2), .out_3(demultiplexer_3_out_3), .out_4(demultiplexer_3_out_4),
    .out_5(demultiplexer_3_out_5), .out_6(demultiplexer_3_out_6), .out_7(demultiplexer_3_out_7));
  D_FF_AS d_ff_as_5 (
    .Set(demultiplexer_1_out_0[4]), .D(D_3[4]), .C(and_9_out), .Clr(demultiplexer_1_out_1[4]), .Q(Q_3[4]),
    .nQ(d_ff_as_5_nq));
  Demultiplexer #(.Selector_Bits(3), .Bits(2)) demultiplexer_4 (
    .sel(LHS[4:2]), .in(LHS[1:0]), .out_0(demultiplexer_4_out_0), .out_1(demultiplexer_4_out_1),
    .out_2(demultiplexer_4_out_2), .out_3(demultiplexer_4_out_3), .out_4(demultiplexer_4_out_4),
    .out_5(demultiplexer_4_out_5), .out_6(demultiplexer_4_out_6), .out_7(demultiplexer_4_out_7));
  D_FF_AS d_ff_as_6 (
    .Set(demultiplexer_1_out_0[5]), .D(D_3[5]), .C(and_9_out), .Clr(demultiplexer_1_out_1[5]), .Q(Q_3[5]),
    .nQ(d_ff_as_6_nq));
  D_FF_AS d_ff_as_7 (
    .Set(demultiplexer_1_out_0[6]), .D(D_3[6]), .C(and_9_out), .Clr(demultiplexer_1_out_1[6]), .Q(DIR));  // open: nQ
  Demultiplexer #(.Selector_Bits(3), .Bits(4)) demultiplexer_5 (
    .sel(OPS[6:4]), .in(OPS[3:0]), .out_0(demultiplexer_5_out_0), .out_1(demultiplexer_5_out_1),
    .out_2(demultiplexer_5_out_2), .out_3(demultiplexer_5_out_3), .out_4(demultiplexer_5_out_4),
    .out_5(demultiplexer_5_out_5), .out_6(demultiplexer_5_out_6), .out_7(demultiplexer_5_out_7));
  D_FF_AS d_ff_as_8 (
    .Set(demultiplexer_1_out_0[7]), .D(D_3[7]), .C(and_9_out), .Clr(demultiplexer_1_out_1[7]), .Q(INTA));  // open: nQ
  or or_4 (or_4_out, Q_3[1], Q_3[3]);
  and and_10 (and_10_out, d_ff_as_2_nq, d_ff_as_4_nq);
  xor xor_2 (xor_2_out, Q_3[4], Q_3[2]);
  xnor xnor_1 (xnor_1_out, Q_3[4], Q_3[2]);
  Decoder #(.Selector_Bits(3)) decoder_2 (
    .sel(INDS), .out_0(decoder_2_out_0[0]), .out_1(decoder_2_out_0[1]), .out_2(decoder_2_out_0[2]),
    .out_3(decoder_2_out_0[3]), .out_4(decoder_2_out_0[4]), .out_5(decoder_2_out_0[5]),
    .out_6(decoder_2_out_0[6]), .out_7(decoder_2_out_0[7]));
  or or_5 (or_5_out, xor_2_out, Q_3[3]);
  and and_11 (and_11_out, xnor_1_out, d_ff_as_4_nq);
  Decoder #(.Selector_Bits(3)) decoder_3 (
    .sel(BAS), .out_0(decoder_3_out_0[0]), .out_1(decoder_3_out_0[1]), .out_2(decoder_3_out_0[2]),
    .out_3(decoder_3_out_0[3]), .out_4(decoder_3_out_0[4]), .out_5(decoder_3_out_0[5]),
    .out_6(decoder_3_out_0[6]), .out_7(decoder_3_out_0[7]));
  Multiplexer #(.Selector_Bits(4)) multiplexer_9 (
    .sel(FJS), .in_0(Q_3[5]), .in_1(d_ff_as_6_nq), .in_2(Q_3[4]), .in_3(d_ff_as_5_nq), .in_4(Q_3[3]),
    .in_5(d_ff_as_4_nq), .in_6(Q_3[2]), .in_7(d_ff_as_3_nq), .in_8(Q_3[1]), .in_9(d_ff_as_2_nq),
    .in_10(or_4_out), .in_11(and_10_out), .in_12(xor_2_out), .in_13(xnor_1_out), .in_14(or_5_out),
    .in_15(and_11_out), .out(RES));
  or or_6 (or_6_out, demultiplexer_2_out_0[1], demultiplexer_2_out_0[0]);
  or or_7 (or_7_out, demultiplexer_3_out_0[1], demultiplexer_3_out_0[0]);
  or or_8 (or_8_out, demultiplexer_4_out_0[1], demultiplexer_4_out_0[0]);
  _16_bit_GPR _16_bit_gpr_1 (
    .D(Q), .clk(xclk), .OPS(demultiplexer_5_out_0), .LHS(demultiplexer_4_out_0), .RHS(demultiplexer_3_out_0),
    .OES(demultiplexer_2_out_0), .RHQ(_16_bit_gpr_1_rhq), .LHQ(_16_bit_gpr_1_lhq), .DBQ(_16_bit_gpr_1_dbq),
    .Q0(_16_bit_gpr_1_q0), .Q1(_16_bit_gpr_1_q1));  // open: CO
  assign LHQ = or_8_out ? _16_bit_gpr_1_lhq : 16'bz;  // Driver driver_7
  assign Q = or_6_out ? _16_bit_gpr_1_dbq : 16'bz;  // Driver driver_8
  assign RHQ = or_7_out ? _16_bit_gpr_1_rhq : 16'bz;  // Driver driver_9
  assign NDQ = decoder_2_out_0[0] ? _16_bit_gpr_1_q1 : 16'bz;  // Driver driver_10
  assign BAQ = decoder_3_out_0[0] ? _16_bit_gpr_1_q0 : 16'bz;  // Driver driver_11
  or or_9 (or_9_out, demultiplexer_2_out_1[1], demultiplexer_2_out_1[0]);
  or or_10 (or_10_out, demultiplexer_3_out_1[1], demultiplexer_3_out_1[0]);
  or or_11 (or_11_out, demultiplexer_4_out_1[1], demultiplexer_4_out_1[0]);
  _16_bit_GPR _16_bit_gpr_2 (
    .D(Q), .clk(xclk), .OPS(demultiplexer_5_out_1), .LHS(demultiplexer_4_out_1), .RHS(demultiplexer_3_out_1),
    .OES(demultiplexer_2_out_1), .RHQ(_16_bit_gpr_2_rhq), .LHQ(_16_bit_gpr_2_lhq), .DBQ(_16_bit_gpr_2_dbq),
    .Q0(_16_bit_gpr_2_q0), .Q1(_16_bit_gpr_2_q1));  // open: CO
  assign LHQ = or_11_out ? _16_bit_gpr_2_lhq : 16'bz;  // Driver driver_12
  assign Q = or_9_out ? _16_bit_gpr_2_dbq : 16'bz;  // Driver driver_13
  assign RHQ = or_10_out ? _16_bit_gpr_2_rhq : 16'bz;  // Driver driver_14
  assign NDQ = decoder_2_out_0[1] ? _16_bit_gpr_2_q1 : 16'bz;  // Driver driver_15
  Multiplexer #(.Bits(8)) multiplexer_10 (.sel(FEN), .in_0({8{1'b0}}), .in_1(D_2), .out(multiplexer_10_out));
  assign BAQ = decoder_3_out_0[1] ? _16_bit_gpr_2_q0 : 16'bz;  // Driver driver_16
  Delay delay_2 (.in(FEN), .out(delay_2_out));
  D_FF #(.Bits(8)) d_ff_1 (.D(multiplexer_10_out), .C(driver_18_out), .Q(d_ff_1_q));  // open: nQ
  assign driver_17_out = xclk ? or_12_out : 1'bz;  // Driver driver_17
  D_FF #(.Bits(8)) d_ff_2 (.D(D_2), .C(driver_17_out), .Q(d_ff_2_q));  // open: nQ
  D_FF #(.Bits(8)) d_ff_3 (.D(d_ff_2_q), .C(driver_17_out), .Q(d_ff_3_q));  // open: nQ
  D_FF #(.Bits(8)) d_ff_4 (.D(d_ff_3_q), .C(driver_17_out), .Q(d_ff_4_q));  // open: nQ
  D_FF #(.Bits(8)) d_ff_5 (.D(d_ff_4_q), .C(driver_17_out), .Q(d_ff_5_q));  // open: nQ
  assign driver_18_out = delay_2_out ? xclk : 1'bz;  // Driver driver_18
  PullDown pulldown_6 (.out(driver_18_out));
  or or_12 (or_12_out, P1, P0);
  or or_13 (or_13_out, demultiplexer_2_out_2[1], demultiplexer_2_out_2[0]);
  or or_14 (or_14_out, demultiplexer_3_out_2[1], demultiplexer_3_out_2[0]);
  or or_15 (or_15_out, demultiplexer_4_out_2[1], demultiplexer_4_out_2[0]);
  _16_bit_GPR _16_bit_gpr_3 (
    .D(Q), .clk(xclk), .OPS(demultiplexer_5_out_2), .LHS(demultiplexer_4_out_2), .RHS(demultiplexer_3_out_2),
    .OES(demultiplexer_2_out_2), .RHQ(_16_bit_gpr_3_rhq), .LHQ(_16_bit_gpr_3_lhq), .DBQ(_16_bit_gpr_3_dbq),
    .Q0(_16_bit_gpr_3_q0), .Q1(_16_bit_gpr_3_q1));  // open: CO
  assign LHQ = or_15_out ? _16_bit_gpr_3_lhq : 16'bz;  // Driver driver_19
  assign Q = or_13_out ? _16_bit_gpr_3_dbq : 16'bz;  // Driver driver_20
  assign RHQ = or_14_out ? _16_bit_gpr_3_rhq : 16'bz;  // Driver driver_21
  assign NDQ = decoder_2_out_0[2] ? _16_bit_gpr_3_q1 : 16'bz;  // Driver driver_22
  ROM #(.AddrBits(16), .isProgramMemory("true"), .Bits(24)) rom_1 (.A({Flags, d_ff_1_q}), .sel(1'b1), .D(rom_1_d));
  ROM #(.AddrBits(16), .isProgramMemory("true"), .Bits(24)) rom_2 (.A({Flags, d_ff_1_q}), .sel(1'b1), .D(rom_2_d));
  ROM #(.AddrBits(16), .isProgramMemory("true"), .Bits(24)) rom_3 (.A({Flags, d_ff_1_q}), .sel(1'b1), .D(rom_3_d));
  assign BAQ = decoder_3_out_0[2] ? _16_bit_gpr_3_q0 : 16'bz;  // Driver driver_23
  or or_16 (or_16_out, demultiplexer_2_out_3[1], demultiplexer_2_out_3[0]);
  or or_17 (or_17_out, demultiplexer_3_out_3[1], demultiplexer_3_out_3[0]);
  or or_18 (or_18_out, demultiplexer_4_out_3[1], demultiplexer_4_out_3[0]);
  _16_bit_GPR _16_bit_gpr_4 (
    .D(Q), .clk(xclk), .OPS(demultiplexer_5_out_3), .LHS(demultiplexer_4_out_3), .RHS(demultiplexer_3_out_3),
    .OES(demultiplexer_2_out_3), .RHQ(_16_bit_gpr_4_rhq), .LHQ(_16_bit_gpr_4_lhq), .DBQ(_16_bit_gpr_4_dbq),
    .Q0(_16_bit_gpr_4_q0), .Q1(_16_bit_gpr_4_q1));  // open: CO
  D_FF #(.Bits(24)) d_ff_6 (.D(rom_1_d), .C(clk_t), .Q(d_ff_6_q));  // open: nQ
  D_FF #(.Bits(24)) d_ff_7 (.D(rom_2_d), .C(clk_t), .Q(d_ff_7_q));  // open: nQ
  D_FF #(.Bits(24)) d_ff_8 (.D(rom_3_d), .C(clk_t), .Q(d_ff_8_q));  // open: nQ
  assign LHQ = or_18_out ? _16_bit_gpr_4_lhq : 16'bz;  // Driver driver_24
  D_FF #(.Bits(8)) d_ff_9 (.D(d_ff_2_q), .C(clk_t), .Q(d_ff_9_q));  // open: nQ
  D_FF #(.Bits(8)) d_ff_10 (.D(d_ff_3_q), .C(clk_t), .Q(d_ff_10_q));  // open: nQ
  D_FF #(.Bits(8)) d_ff_11 (.D(d_ff_4_q), .C(clk_t), .Q(d_ff_11_q));  // open: nQ
  D_FF #(.Bits(8)) d_ff_12 (.D(d_ff_5_q), .C(clk_t), .Q(d_ff_12_q));  // open: nQ
  assign Q = or_16_out ? _16_bit_gpr_4_dbq : 16'bz;  // Driver driver_25
  assign RHQ = or_17_out ? _16_bit_gpr_4_rhq : 16'bz;  // Driver driver_26
  assign NDQ = decoder_2_out_0[3] ? _16_bit_gpr_4_q1 : 16'bz;  // Driver driver_27
  assign BAQ = decoder_3_out_0[3] ? _16_bit_gpr_4_q0 : 16'bz;  // Driver driver_28
  or or_19 (or_19_out, demultiplexer_2_out_4[1], demultiplexer_2_out_4[0]);
  or or_20 (or_20_out, demultiplexer_3_out_4[1], demultiplexer_3_out_4[0]);
  or or_21 (or_21_out, demultiplexer_4_out_4[1], demultiplexer_4_out_4[0]);
  _16_bit_GPR _16_bit_gpr_5 (
    .D(Q), .clk(xclk), .OPS(demultiplexer_5_out_4), .LHS(demultiplexer_4_out_4), .RHS(demultiplexer_3_out_4),
    .OES(demultiplexer_2_out_4), .RHQ(_16_bit_gpr_5_rhq), .LHQ(_16_bit_gpr_5_lhq), .DBQ(_16_bit_gpr_5_dbq),
    .Q0(_16_bit_gpr_5_q0), .Q1(_16_bit_gpr_5_q1));  // open: CO
  assign LHQ = or_21_out ? _16_bit_gpr_5_lhq : 16'bz;  // Driver driver_29
  D_FF #(.Bits(24)) d_ff_13 (.D(d_ff_6_q), .C(clk_t), .Q(d_ff_13_q));  // open: nQ
  D_FF #(.Bits(24)) d_ff_14 (.D(d_ff_7_q), .C(clk_t), .Q(d_ff_14_q));  // open: nQ
  D_FF #(.Bits(24)) d_ff_15 (.D(d_ff_8_q), .C(clk_t), .Q(d_ff_15_q));  // open: nQ
  assign Q = or_19_out ? _16_bit_gpr_5_dbq : 16'bz;  // Driver driver_30
  assign RHQ = or_20_out ? _16_bit_gpr_5_rhq : 16'bz;  // Driver driver_31
  assign NDQ = decoder_2_out_0[4] ? _16_bit_gpr_5_q1 : 16'bz;  // Driver driver_32
  D_FF #(.Bits(8)) d_ff_16 (.D(d_ff_9_q), .C(clk_t), .Q(d_ff_16_q));  // open: nQ
  D_FF #(.Bits(8)) d_ff_17 (.D(d_ff_10_q), .C(clk_t), .Q(d_ff_17_q));  // open: nQ
  D_FF #(.Bits(8)) d_ff_18 (.D(d_ff_11_q), .C(clk_t), .Q(d_ff_18_q));  // open: nQ
  D_FF #(.Bits(8)) d_ff_19 (.D(d_ff_12_q), .C(clk_t), .Q(d_ff_19_q));  // open: nQ
  assign BAQ = decoder_3_out_0[4] ? _16_bit_gpr_5_q0 : 16'bz;  // Driver driver_33
  or or_22 (or_22_out, demultiplexer_2_out_5[1], demultiplexer_2_out_5[0]);
  or or_23 (or_23_out, demultiplexer_3_out_5[1], demultiplexer_3_out_5[0]);
  or or_24 (or_24_out, demultiplexer_4_out_5[1], demultiplexer_4_out_5[0]);
  _16_bit_GPR _16_bit_gpr_6 (
    .D(Q), .clk(xclk), .OPS(demultiplexer_5_out_5), .LHS(demultiplexer_4_out_5), .RHS(demultiplexer_3_out_5),
    .OES(demultiplexer_2_out_5), .RHQ(_16_bit_gpr_6_rhq), .LHQ(_16_bit_gpr_6_lhq), .DBQ(_16_bit_gpr_6_dbq),
    .Q0(_16_bit_gpr_6_q0), .Q1(_16_bit_gpr_6_q1));  // open: CO
  assign LHQ = or_24_out ? _16_bit_gpr_6_lhq : 16'bz;  // Driver driver_34
  assign Q = or_22_out ? _16_bit_gpr_6_dbq : 16'bz;  // Driver driver_35
  assign RHQ = or_23_out ? _16_bit_gpr_6_rhq : 16'bz;  // Driver driver_36
  assign NDQ = decoder_2_out_0[5] ? _16_bit_gpr_6_q1 : 16'bz;  // Driver driver_37
  assign BAQ = decoder_3_out_0[5] ? _16_bit_gpr_6_q0 : 16'bz;  // Driver driver_38
  D_FF #(.Bits(24)) d_ff_20 (.D(d_ff_13_q), .C(clk_t), .Q(uOP_0));  // open: nQ
  D_FF #(.Bits(24)) d_ff_21 (.D(d_ff_14_q), .C(clk_t), .Q(uOP_1));  // open: nQ
  D_FF #(.Bits(24)) d_ff_22 (.D(d_ff_15_q), .C(clk_t), .Q(uOP_2));  // open: nQ
  D_FF #(.Bits(8)) d_ff_23 (.D(d_ff_16_q), .C(clk_t), .Q(ST_0));  // open: nQ
  D_FF #(.Bits(8)) d_ff_24 (.D(d_ff_17_q), .C(clk_t), .Q(ST_1));  // open: nQ
  D_FF #(.Bits(8)) d_ff_25 (.D(d_ff_18_q), .C(clk_t), .Q(ST_2));  // open: nQ
  D_FF #(.Bits(8)) d_ff_26 (.D(d_ff_19_q), .C(clk_t), .Q(ST_3));  // open: nQ
  or or_25 (or_25_out, demultiplexer_2_out_6[1], demultiplexer_2_out_6[0]);
  or or_26 (or_26_out, demultiplexer_3_out_6[1], demultiplexer_3_out_6[0]);
  or or_27 (or_27_out, demultiplexer_4_out_6[1], demultiplexer_4_out_6[0]);
  _16_bit_GPR _16_bit_gpr_7 (
    .D(Q), .clk(xclk), .OPS(demultiplexer_5_out_6), .LHS(demultiplexer_4_out_6), .RHS(demultiplexer_3_out_6),
    .OES(demultiplexer_2_out_6), .RHQ(_16_bit_gpr_7_rhq), .LHQ(_16_bit_gpr_7_lhq), .DBQ(_16_bit_gpr_7_dbq),
    .Q0(_16_bit_gpr_7_q0), .Q1(_16_bit_gpr_7_q1));  // open: CO
  assign LHQ = or_27_out ? _16_bit_gpr_7_lhq : 16'bz;  // Driver driver_39
  assign Q = or_25_out ? _16_bit_gpr_7_dbq : 16'bz;  // Driver driver_40
  assign RHQ = or_26_out ? _16_bit_gpr_7_rhq : 16'bz;  // Driver driver_41
  assign NDQ = decoder_2_out_0[6] ? _16_bit_gpr_7_q1 : 16'bz;  // Driver driver_42
  assign BAQ = decoder_3_out_0[6] ? _16_bit_gpr_7_q0 : 16'bz;  // Driver driver_43
  or or_28 (or_28_out, demultiplexer_2_out_7[15], demultiplexer_2_out_7[14]);
  or or_29 (or_29_out, demultiplexer_3_out_7[15], demultiplexer_3_out_7[14]);
  or or_30 (or_30_out, demultiplexer_4_out_7[15], demultiplexer_4_out_7[14]);
  _16_bit_GPR _16_bit_gpr_8 (
    .D(Q), .clk(xclk), .OPS(demultiplexer_5_out_7), .LHS(demultiplexer_4_out_7), .RHS(demultiplexer_3_out_7),
    .OES(demultiplexer_2_out_7), .RHQ(_16_bit_gpr_8_rhq), .LHQ(_16_bit_gpr_8_lhq), .DBQ(_16_bit_gpr_8_dbq),
    .Q0(_16_bit_gpr_8_q0), .Q1(_16_bit_gpr_8_q1));  // open: CO
  assign LHQ = or_30_out ? _16_bit_gpr_8_lhq : 16'bz;  // Driver driver_44
  assign Q = or_28_out ? _16_bit_gpr_8_dbq : 16'bz;  // Driver driver_45
  assign RHQ = or_29_out ? _16_bit_gpr_8_rhq : 16'bz;  // Driver driver_46
  assign NDQ = decoder_2_out_0[7] ? _16_bit_gpr_8_q1 : 16'bz;  // Driver driver_47
  assign BAQ = decoder_3_out_0[7] ? _16_bit_gpr_8_q0 : 16'bz;  // Driver driver_48

  assign Q_2[15] = FO[2];
  assign Q_3[7:6] = {INTA, DIR};

  // Other names for the same wires on the sheet: sel[4:0] = OP

  // Notes on the sheet:
  //   D: Data In
  //   RHS: Register Select Bits (2-4):
  //   000 - AX
  //   001 - CX
  //   010 - DX
  //   011 - BX
  //   100 - SP
  //   101 - BP
  //   110 - SI
  //   111 - DI
  //   Right Hand Side Output Select: (Bits 0-1)
  //   00 - NOP
  //   01 - Lower byte of GPR
  //   10 - Upper byte of GPR
  //   11 - Full value of GPR
  //   LHS: Register Select Bits (2-4):
  //   000 - AX
  //   001 - CX
  //   010 - DX
  //   011 - BX
  //   100 - SP
  //   101 - BP
  //   110 - SI
  //   111 - DI
  //   Left Hand Side Output Select:
  //   00 - NOP
  //   01 - Lower byte of GPR
  //   10 - Upper byte of GPR
  //   11 - Full value of GPR
  //   OES: Register Select Bits (2-4):
  //   000 - AX
  //   001 - CX
  //   010 - DX
  //   011 - BX
  //   100 - SP
  //   101 - BP
  //   110 - SI
  //   111 - DI
  //   Output Select Bits (0-1):
  //   00 - NOP
  //   01 - Lower byte of GPR
  //   10 - Upper byte of GPR
  //   11 - Full value of GPR
  //   GPRI: General Purpose Register Block 
  //    - Data Bus In
  //   OPS: Register Select Bits (4-6):
  //   000 - AX
  //   001 - CX
  //   010 - DX
  //   011 - BX
  //   100 - SP
  //   101 - BP
  //   110 - SI
  //   111 - DI
  //   Instruction Bits (0-3):
  //   0000 - NOP
  //   0001 - Load value into GPR
  //   0010 - Increment-LowByte
  //   0011 - Decrement-LowByte
  //   0100 - Load GPR-LowByte
  //   0101 - Load GPR-UpperByte
  //   0110 - Increment-UpperByte
  //   0111 - Decrement-UpperByte
  //   1000 - NOP
  //   1001 - C2Invert GPR
  //   1010 - C2Invert-LowByte
  //   1011 - C2Invert-UpperByte
  //   1100 - NOP
  //   1101 - NOP
  //   1110 - Increment GPR
  //   1111 - Decrement GPR
  //   INDS: Index Address Select:
  //   000 - AX
  //   001 - CX
  //   010 - DX
  //   011 - BX
  //   100 - SP
  //   101 - BP
  //   110 - SI
  //   111 - DI
  //   BAS: Base Address Select:
  //   000 - AX
  //   001 - CX
  //   010 - DX
  //   011 - BX
  //   100 - SP
  //   101 - BP
  //   110 - SI
  //   111 - DI
  //   P0: Push a value onto the Data Stack
  //   Q: result of the operation
  //   {{de Ergebnis der Operation}}
  //   RHQ: result of the operation
  //   {{de Ergebnis der Operation}}
  //   LHQ: result of the operation
  //   {{de Ergebnis der Operation}}
  //   BAQ: result of the operation
  //   {{de Ergebnis der Operation}}
  //   NDQ: Index Address Out
  //   clk_2: Hz: 65536
  //   FEN: Fetch Instruction Enable
  //   ST_0: result of the operation
  //   {{de Ergebnis der Operation}}
  //   ST_1: result of the operation
  //   {{de Ergebnis der Operation}}
  //   ST_2: result of the operation
  //   {{de Ergebnis der Operation}}
  //   ST_3: Index Address Out
  //   P1: Push a value onto the Data Stack
  //   D_2: Data In
  //   uOP_0: result of the operation
  //   {{de Ergebnis der Operation}}
  //   uOP_1: result of the operation
  //   {{de Ergebnis der Operation}}
  //   uOP_2: result of the operation
  //   {{de Ergebnis der Operation}}
  //   A: first operand
  //   B: second operand
  //   OP: Operation Select:
  //   00000 - ADD (Add)
  //   00001 - ADC16 (Add with carry)
  //   00010 - NOT
  //   00011 - SBC16 (Subtract with borrow)
  //   00100 - XOR
  //   00101 - INCC16 (Increment on Carry)
  //   00110 - DEC (Decrement LHS)
  //   00111 - DECC16 (Decrement on Carry)
  //   01000 - AND
  //   01001 - nop
  //   01010 - OR
  //   01011 - CMP16
  //   01100 - INC (Increment LHS)
  //   01101 - nop
  //   01110 - SUB (Subtract)
  //   01111 - CMP8
  //   10000 - SHL16
  //   10001 - SHR16
  //   10010 - BSF
  //   10011 - ASR16
  //   10100 - ROL16
  //   10101 - ROR16
  //   10110 - RCL16
  //   10111 - RCR16
  //   11000 - SHL8
  //   11001 - SHR8
  //   11010 - BSR
  //   11011 - ASR8
  //   11100 - ROL8
  //   11101 - ROR8
  //   11110 - RCL8
  //   11111 - RCR8
  //   Q_2: result of the operation
  //   {{de Ergebnis der Operation}}
  //   FO: Is high if the result is negative.
  //   {{de Ist High wenn das Ergebnis negativ ist.}}
  //   FI: Flags Input:
  //   first - carry
  //   second - zero
  //   third - negative
  //   fourth - overflow
  //   FS: Flag Operation Select
  //   Mode Bit [0]:
  //   0 - Set
  //   1 - Reset
  //   Flag Select[1-3]:
  //   000 - none
  //   001 - Carry
  //   010 - Overflow
  //   011 - Zero
  //   100 - Sign
  //   101 - Parity
  //   110 - Direction
  //   111 - Interrupt
  //   L: Flag Register Write/Latch Data
  //   D_3: Flag Data In
  //   Q_3: Flags Data Out
  //   FJS: Flag Jump Select:
  //   00000 - JP
  //   00001 - JNP
  //   00010 - JS
  //   00011 - JNS
  //   00100 - JZ
  //   00101 - JNZ
  //   00110 - JO
  //   00111 - JNO
  //   01000 - JC/JNAE/JB
  //   01001 - JNC/JAE/JNB
  //   01010 - JBE/JNA
  //   01011 - JNBE/JA
  //   01100 - JL/JNGE
  //   01101 - JNL/JGE
  //   01110 - JLE/JNG
  //   01111 - JNLE/JG
  //   INTA: Interrupt Allow
  //   0 - Do not Allow
  //   1 - Allow
  //   DIR: Direction of String Instructions
  //   0 - Increment SI/DI
  //   1 - Decrement SI/DI
  //   RES: Result of Flag Filtering
  //   Clk_3: Clock
  //   ARITHMETIC/LOGIC UNIT
  //   CLOCK
  //   N
  //   C
  //   FLAGS UNIT
  //   O
  //   Z
  //   S
  //   P
  //   D
  //   I
  //   AX
  //   CX
  //   FETCH&DECODE
  //   FETCH STAGE
  //   DATA STACK
  //   DX
  //   contents of rom_1 (hex, n*v repeats v):
  //   fff000000000,1,2,3,4,5,6,7
  //   contents of rom_2 (hex, n*v repeats v):
  //   fff000000000,1,2,3,4,5,6,7
  //   contents of rom_3 (hex, n*v repeats v):
  //   fff000000000,1,2,3,4,5,6,7
  //   BX
  //   REGISTER PAGE
  //   SP
  //   PIPELINE STAGES
  //   BP
  //   SI
  //   DI
endmodule
